// Digital circuit ALU.dig as structural Verilog
module ALU (
  input  INP11,
  input  INP10,
  input  INP9,
  input  INP8,
  input  A,
  input  B,
  input  S_select,
  input  D1_9,
  input  D0_10,
  input  D0_11,
  input  D0_12,
  input  D0_13,
  input  D0_14,
  input  D0_15,
  input  S_select_2,
  output _15_alu,
  output _14_alu,
  output _13_alu,
  output _12_alu,
  output _11_alu,
  output _10_alu,
  output _9_alu,
  output _8_alu,
  output _7_alu,
  output _6_alu,
  output _5_alu,
  output _4_alu,
  output _3_alu,
  output _2_alu,
  output _1_sub,
  output _0_alu,
  output out_31,
  output OUT16,
  output OUT17,
  output OUT18,
  output OUT19,
  output OUT20,
  output OUT21,
  output OUT22,
  output OUT23
);

  wire nand_1_out, nand_2_out, nand_3_out, nand_4_out, nand_5_out, nand_6_out, nand_7_out, nand_8_out,
       nand_9_out, nand_10_out, nand_11_out, nand_12_out, nand_13_out, nand_14_out, nand_15_out, nand_16_out,
       nand_17_out, nand_18_out, nand_19_out, nand_20_out, nand_21_out, nand_22_out, nand_23_out,
       nand_24_out, nand_25_out, nand_26_out, nand_27_out, nand_28_out, nand_29_out, nand_30_out,
       nand_31_out, nand_32_out, nand_33_out, nand_34_out, nand_35_out, nand_36_out, nand_37_out,
       nand_38_out, nand_39_out, nand_40_out, nand_41_out, nand_42_out, nand_43_out, nand_44_out,
       nand_45_out, nand_46_out, nand_47_out, nand_48_out, nand_49_out, nand_50_out, nand_51_out,
       nand_52_out, nand_53_out, nand_54_out, nand_55_out, nand_56_out, nand_57_out, nand_58_out,
       nand_59_out, nand_60_out, nand_61_out, nand_62_out, nand_63_out, nand_64_out, nand_65_out,
       nand_66_out, nand_67_out, nand_68_out, nand_69_out, nand_70_out, nand_71_out, nand_72_out,
       nand_73_out, nand_74_out, nand_75_out, nand_76_out, nand_77_out, nand_78_out, nand_79_out,
       nand_80_out, nand_81_out, nand_82_out, nand_83_out, nand_84_out, nand_85_out, nand_86_out,
       nand_87_out, nand_88_out, nand_89_out, nand_90_out, nand_91_out, nand_92_out, nand_93_out,
       nand_94_out, nand_95_out, nand_96_out, nand_97_out, nand_98_out, nand_99_out, nand_100_out,
       nand_101_out, nand_102_out, nand_103_out, nand_104_out, nand_105_out, nand_106_out, nand_107_out,
       nand_108_out, nand_109_out, nand_110_out, nand_111_out, nand_112_out, nand_113_out, nand_114_out,
       nand_115_out, nand_116_out, nand_117_out, nand_118_out, nand_119_out, nand_120_out, nand_121_out,
       nand_122_out, nand_123_out, nand_124_out, nand_125_out, nand_126_out, nand_127_out, nand_128_out,
       nand_129_out, nand_130_out, nand_131_out, nand_132_out, nand_133_out, nand_134_out, nand_135_out,
       nand_136_out, nand_137_out, nand_138_out, nand_139_out, nand_140_out, nand_141_out, nand_142_out,
       nand_143_out, nand_144_out, nand_145_out, nand_146_out, nand_147_out, nand_148_out, nand_149_out,
       nand_150_out, nand_151_out, nand_152_out, nand_153_out, nand_154_out, nand_155_out, nand_156_out,
       nand_157_out, nand_158_out, nand_159_out, nand_160_out, nor_1_out, nor_2_out, nor_3_out, nor_4_out,
       nor_5_out, nor_6_out, nor_7_out, nor_8_out, nor_9_out, nor_10_out, nor_11_out, nor_12_out, nor_13_out,
       nor_14_out, nor_15_out, nor_16_out, nor_17_out, nor_18_out, nor_19_out, nor_20_out, nor_21_out,
       nor_22_out, nor_23_out, nor_24_out, nor_25_out, nor_26_out, nor_27_out, nor_28_out, nor_29_out,
       nor_30_out, nor_31_out, nor_32_out, nor_33_out, nor_34_out, nor_35_out, nor_36_out, nor_37_out,
       nor_38_out, nor_39_out, nor_40_out, nor_41_out, nor_42_out, nor_43_out, nor_44_out, nor_45_out,
       nor_46_out, nor_47_out, nor_48_out, nor_49_out, nor_50_out, nor_51_out, nor_52_out, nor_53_out,
       nor_54_out, nor_55_out, nor_56_out, nor_57_out, nor_58_out, nor_59_out, nor_60_out, nor_61_out,
       nor_62_out, nor_63_out, nor_64_out, not_2_out, not_8_out, not_13_out, not_20_out, not_21_out,
       not_22_out, not_23_out, not_24_out, not_25_out, not_26_out, not_27_out, not_28_out, not_29_out,
       not_30_out, not_31_out, not_32_out, not_33_out, not_34_out, not_35_out, not_36_out, not_37_out,
       not_38_out, not_39_out, not_40_out, not_41_out, not_42_out, not_43_out, not_44_out, not_45_out,
       not_46_out, not_47_out, not_48_out, not_49_out, not_50_out, not_51_out, not_52_out, not_53_out,
       not_54_out, not_55_out, not_56_out, not_57_out, not_58_out, not_59_out, not_60_out, not_61_out,
       not_62_out, not_63_out, not_64_out, not_65_out, not_66_out, not_67_out, not_68_out, not_69_out,
       not_70_out, not_71_out, not_72_out, not_73_out, not_74_out, not_75_out, not_76_out, not_77_out,
       not_78_out, not_79_out, not_80_out, not_81_out, not_82_out, not_83_out, not_84_out, not_85_out,
       not_86_out, not_87_out, not_88_out, not_89_out, not_90_out, not_91_out, not_92_out, not_93_out,
       not_94_out, not_95_out, not_96_out, not_97_out, not_98_out, not_99_out, not_100_out, not_101_out,
       not_102_out, not_103_out, not_104_out, not_105_out, not_106_out, not_107_out, not_108_out,
       not_109_out, not_110_out, not_111_out, not_112_out, not_113_out, not_114_out, not_115_out,
       not_116_out, not_117_out, not_118_out, not_119_out, not_120_out, not_121_out, not_122_out,
       not_123_out, not_124_out, not_125_out, not_126_out, not_127_out, not_128_out, not_129_out,
       not_130_out, not_131_out, not_132_out, not_133_out, not_134_out, not_135_out, not_136_out,
       not_137_out, not_138_out, not_139_out, not_140_out, not_141_out, not_142_out, not_143_out,
       not_144_out, not_145_out, not_146_out, not_147_out, not_148_out, not_149_out, not_150_out,
       not_151_out, not_152_out, not_153_out, not_154_out, not_155_out, not_156_out, not_157_out,
       not_158_out, not_159_out, not_160_out, not_161_out, not_162_out, not_163_out, not_164_out,
       not_165_out, not_166_out, not_167_out, not_168_out, not_169_out, not_170_out, not_171_out,
       not_172_out, not_173_out, not_174_out, not_175_out, not_176_out, not_177_out, not_178_out,
       not_179_out, not_181_out, not_182_out, not_183_out, not_184_out, not_185_out, not_186_out,
       not_187_out, not_188_out, not_189_out, not_190_out, not_191_out, not_192_out, not_193_out,
       not_194_out, not_195_out, not_196_out, not_197_out, not_198_out, not_199_out, not_200_out,
       not_201_out, not_202_out, not_203_out, not_204_out, not_205_out, not_206_out, not_207_out,
       not_208_out, not_209_out, not_210_out, not_211_out, not_212_out, not_213_out, not_214_out,
       not_215_out, not_216_out, not_217_out, not_218_out, not_219_out, not_220_out, not_221_out,
       not_222_out, not_223_out, not_224_out, not_225_out, not_226_out, not_227_out, not_228_out,
       not_229_out, not_230_out, not_231_out, not_232_out, not_233_out, not_234_out, not_235_out,
       not_236_out, not_237_out, not_238_out, not_239_out, not_240_out, not_241_out, not_242_out,
       not_243_out, not_244_out, not_245_out, not_246_out, not_247_out, not_248_out, not_249_out,
       not_250_out, not_251_out, not_252_out, not_253_out, not_254_out, not_255_out, not_256_out,
       not_257_out, not_258_out, not_259_out, not_260_out, not_261_out, not_262_out, not_263_out,
       not_264_out, not_265_out, not_266_out, not_267_out, not_268_out, not_269_out, not_270_out,
       not_271_out, not_272_out;

  not not_1 (_15_alu, nand_1_out);
  not not_2 (not_2_out, INP11);
  nand nand_1 (nand_1_out, INP8, INP9, INP10, INP11);
  nand nand_2 (nand_2_out, not_20_out, INP9, INP10, INP11);
  not not_3 (_14_alu, nand_2_out);
  not not_4 (_13_alu, nand_3_out);
  nand nand_3 (nand_3_out, INP8, not_13_out, INP10, INP11);
  nand nand_4 (nand_4_out, not_20_out, not_13_out, INP10, INP11);
  not not_5 (_12_alu, nand_4_out);
  not not_6 (_11_alu, nand_5_out);
  nand nand_5 (nand_5_out, INP8, INP9, not_8_out, INP11);
  nand nand_6 (nand_6_out, not_20_out, INP9, not_8_out, INP11);
  not not_7 (_10_alu, nand_6_out);
  not not_8 (not_8_out, INP10);
  not not_9 (_9_alu, nand_7_out);
  nand nand_7 (nand_7_out, INP8, not_13_out, not_8_out, INP11);
  nand nand_8 (nand_8_out, not_20_out, not_13_out, not_8_out, INP11);
  not not_10 (_8_alu, nand_8_out);
  nand nand_9 (nand_9_out, INP8, INP9, INP10, not_2_out);
  not not_11 (_7_alu, nand_9_out);
  not not_12 (_6_alu, nand_10_out);
  nand nand_10 (nand_10_out, not_20_out, INP9, INP10, not_2_out);
  not not_13 (not_13_out, INP9);
  nand nand_11 (nand_11_out, INP8, not_13_out, INP10, not_2_out);
  not not_14 (_5_alu, nand_11_out);
  not not_15 (_4_alu, nand_12_out);
  nand nand_12 (nand_12_out, not_20_out, not_13_out, INP10, not_2_out);
  nand nand_13 (nand_13_out, INP8, INP9, not_8_out, not_2_out);
  not not_16 (_3_alu, nand_13_out);
  not not_17 (_2_alu, nand_14_out);
  nand nand_14 (nand_14_out, not_20_out, INP9, not_8_out, not_2_out);
  nand nand_15 (nand_15_out, INP8, not_13_out, not_8_out, not_2_out);
  not not_18 (_1_sub, nand_15_out);
  not not_19 (_0_alu, nand_16_out);
  not not_20 (not_20_out, INP8);
  nand nand_16 (nand_16_out, not_20_out, not_13_out, not_8_out, not_2_out);
  nand nand_17 (nand_17_out, A, B);
  nand nand_18 (nand_18_out, A, B);
  nand nand_19 (nand_19_out, A, B);
  nand nand_20 (nand_20_out, A, B);
  nand nand_21 (nand_21_out, A, B);
  nand nand_22 (nand_22_out, A, B);
  nand nand_23 (nand_23_out, A, B);
  nand nand_24 (nand_24_out, A, B);
  nor nor_1 (nor_1_out, A, B);
  nor nor_2 (nor_2_out, A, B);
  nor nor_3 (nor_3_out, A, B);
  nor nor_4 (nor_4_out, A, B);
  nor nor_5 (nor_5_out, A, B);
  nor nor_6 (nor_6_out, A, B);
  nor nor_7 (nor_7_out, A, B);
  nor nor_8 (nor_8_out, A, B);
  not not_21 (not_21_out, A);
  not not_22 (not_22_out, B);
  not not_23 (not_23_out, A);
  not not_24 (not_24_out, B);
  not not_25 (not_25_out, A);
  not not_26 (not_26_out, B);
  not not_27 (not_27_out, A);
  not not_28 (not_28_out, B);
  not not_29 (not_29_out, A);
  not not_30 (not_30_out, B);
  not not_31 (not_31_out, A);
  not not_32 (not_32_out, B);
  not not_33 (not_33_out, A);
  not not_34 (not_34_out, B);
  not not_35 (not_35_out, A);
  not not_36 (not_36_out, B);
  not not_37 (not_37_out, A);
  not not_38 (not_38_out, B);
  not not_39 (not_39_out, A);
  not not_40 (not_40_out, B);
  not not_41 (not_41_out, A);
  not not_42 (not_42_out, B);
  not not_43 (not_43_out, A);
  not not_44 (not_44_out, B);
  not not_45 (not_45_out, A);
  not not_46 (not_46_out, B);
  not not_47 (not_47_out, A);
  not not_48 (not_48_out, B);
  not not_49 (not_49_out, A);
  not not_50 (not_50_out, B);
  not not_51 (not_51_out, A);
  not not_52 (not_52_out, B);
  nand nand_25 (nand_25_out, A, B);
  nand nand_26 (nand_26_out, A, not_38_out);
  nand nand_27 (nand_27_out, not_37_out, B);
  nand nand_28 (nand_28_out, A, B);
  nand nand_29 (nand_29_out, A, not_40_out);
  nand nand_30 (nand_30_out, not_39_out, B);
  nand nand_31 (nand_31_out, A, B);
  nand nand_32 (nand_32_out, A, not_42_out);
  nand nand_33 (nand_33_out, not_41_out, B);
  nand nand_34 (nand_34_out, A, B);
  nand nand_35 (nand_35_out, A, not_44_out);
  nand nand_36 (nand_36_out, not_43_out, B);
  nand nand_37 (nand_37_out, A, B);
  nand nand_38 (nand_38_out, A, not_46_out);
  nand nand_39 (nand_39_out, not_45_out, B);
  nand nand_40 (nand_40_out, A, B);
  nand nand_41 (nand_41_out, A, not_48_out);
  nand nand_42 (nand_42_out, not_47_out, B);
  nand nand_43 (nand_43_out, A, B);
  nand nand_44 (nand_44_out, A, not_50_out);
  nand nand_45 (nand_45_out, not_49_out, B);
  nand nand_46 (nand_46_out, A, B);
  nand nand_47 (nand_47_out, A, not_52_out);
  nand nand_48 (nand_48_out, not_51_out, B);
  not not_53 (not_53_out, nand_17_out);
  not not_54 (not_54_out, nand_18_out);
  not not_55 (not_55_out, nand_19_out);
  not not_56 (not_56_out, nand_20_out);
  not not_57 (not_57_out, nand_21_out);
  not not_58 (not_58_out, nand_22_out);
  not not_59 (not_59_out, nand_23_out);
  not not_60 (not_60_out, nand_24_out);
  not not_61 (not_61_out, nor_1_out);
  not not_62 (not_62_out, nor_2_out);
  not not_63 (not_63_out, nor_3_out);
  not not_64 (not_64_out, nor_4_out);
  not not_65 (not_65_out, nor_5_out);
  not not_66 (not_66_out, nor_6_out);
  not not_67 (not_67_out, nor_7_out);
  not not_68 (not_68_out, nor_8_out);
  nand nand_49 (nand_49_out, A, not_22_out);
  nand nand_50 (nand_50_out, not_21_out, B);
  nand nand_51 (nand_51_out, A, not_24_out);
  nand nand_52 (nand_52_out, not_23_out, B);
  nand nand_53 (nand_53_out, A, not_26_out);
  nand nand_54 (nand_54_out, not_25_out, B);
  nand nand_55 (nand_55_out, A, not_28_out);
  nand nand_56 (nand_56_out, not_27_out, B);
  nand nand_57 (nand_57_out, A, not_30_out);
  nand nand_58 (nand_58_out, not_29_out, B);
  nand nand_59 (nand_59_out, A, not_32_out);
  nand nand_60 (nand_60_out, not_31_out, B);
  nand nand_61 (nand_61_out, A, not_34_out);
  nand nand_62 (nand_62_out, not_33_out, B);
  nand nand_63 (nand_63_out, A, not_36_out);
  nand nand_64 (nand_64_out, not_35_out, B);
  not not_69 (not_69_out, nand_49_out);
  not not_70 (not_70_out, nand_50_out);
  not not_71 (not_71_out, nand_51_out);
  not not_72 (not_72_out, nand_52_out);
  not not_73 (not_73_out, nand_53_out);
  not not_74 (not_74_out, nand_54_out);
  not not_75 (not_75_out, nand_55_out);
  not not_76 (not_76_out, nand_56_out);
  not not_77 (not_77_out, nand_57_out);
  not not_78 (not_78_out, nand_58_out);
  not not_79 (not_79_out, nand_59_out);
  not not_80 (not_80_out, nand_60_out);
  not not_81 (not_81_out, nand_61_out);
  not not_82 (not_82_out, nand_62_out);
  not not_83 (not_83_out, nand_63_out);
  not not_84 (not_84_out, nand_64_out);
  not not_85 (not_85_out, nand_26_out);
  not not_86 (not_86_out, nand_27_out);
  not not_87 (not_87_out, nand_29_out);
  not not_88 (not_88_out, nand_30_out);
  not not_89 (not_89_out, nand_32_out);
  not not_90 (not_90_out, nand_33_out);
  not not_91 (not_91_out, nand_35_out);
  not not_92 (not_92_out, nand_36_out);
  not not_93 (not_93_out, nand_38_out);
  not not_94 (not_94_out, nand_39_out);
  not not_95 (not_95_out, nand_41_out);
  not not_96 (not_96_out, nand_42_out);
  not not_97 (not_97_out, nand_44_out);
  not not_98 (not_98_out, nand_45_out);
  not not_99 (not_99_out, nand_47_out);
  not not_100 (not_100_out, nand_48_out);
  nor nor_9 (nor_9_out, not_69_out, not_70_out);
  nor nor_10 (nor_10_out, not_71_out, not_72_out);
  nor nor_11 (nor_11_out, not_73_out, not_74_out);
  nor nor_12 (nor_12_out, not_75_out, not_76_out);
  nor nor_13 (nor_13_out, not_77_out, not_78_out);
  nor nor_14 (nor_14_out, not_79_out, not_80_out);
  nor nor_15 (nor_15_out, not_81_out, not_82_out);
  nor nor_16 (nor_16_out, not_83_out, not_84_out);
  nor nor_17 (nor_17_out, not_85_out, not_86_out);
  nor nor_18 (nor_18_out, not_87_out, not_88_out);
  nor nor_19 (nor_19_out, not_89_out, not_90_out);
  nor nor_20 (nor_20_out, not_91_out, not_92_out);
  nor nor_21 (nor_21_out, not_93_out, not_94_out);
  nor nor_22 (nor_22_out, not_95_out, not_96_out);
  nor nor_23 (nor_23_out, not_97_out, not_98_out);
  nor nor_24 (nor_24_out, not_99_out, not_100_out);
  not not_101 (not_101_out, nor_9_out);
  not not_102 (not_102_out, nor_10_out);
  not not_103 (not_103_out, nor_11_out);
  not not_104 (not_104_out, nor_12_out);
  not not_105 (not_105_out, nor_13_out);
  not not_106 (not_106_out, nor_14_out);
  not not_107 (not_107_out, nor_15_out);
  not not_108 (not_108_out, nor_16_out);
  not not_109 (not_109_out, nor_17_out);
  not not_110 (not_110_out, nor_18_out);
  not not_111 (not_111_out, nor_19_out);
  not not_112 (not_112_out, nor_20_out);
  not not_113 (not_113_out, nor_21_out);
  not not_114 (not_114_out, nor_22_out);
  not not_115 (not_115_out, nor_23_out);
  not not_116 (not_116_out, nor_24_out);
  not not_117 (not_117_out, nand_25_out);
  not not_118 (not_118_out, not_109_out);
  not not_119 (not_119_out, 1'b0);
  not not_120 (not_120_out, nand_28_out);
  not not_121 (not_121_out, not_110_out);
  not not_122 (not_122_out, not_166_out);
  not not_123 (not_123_out, nand_31_out);
  not not_124 (not_124_out, not_111_out);
  not not_125 (not_125_out, not_168_out);
  not not_126 (not_126_out, nand_34_out);
  not not_127 (not_127_out, not_112_out);
  not not_128 (not_128_out, not_170_out);
  not not_129 (not_129_out, nand_37_out);
  not not_130 (not_130_out, not_113_out);
  not not_131 (not_131_out, not_172_out);
  not not_132 (not_132_out, nand_40_out);
  not not_133 (not_133_out, not_114_out);
  not not_134 (not_134_out, not_174_out);
  not not_135 (not_135_out, nand_43_out);
  not not_136 (not_136_out, not_115_out);
  not not_137 (not_137_out, not_176_out);
  not not_138 (not_138_out, nand_46_out);
  not not_139 (not_139_out, not_116_out);
  not not_140 (not_140_out, not_178_out);
  nand nand_65 (nand_65_out, not_109_out, not_119_out);
  nand nand_66 (nand_66_out, not_118_out, 1'b0);
  nand nand_67 (nand_67_out, not_109_out, 1'b0);
  nand nand_68 (nand_68_out, not_110_out, not_122_out);
  nand nand_69 (nand_69_out, not_121_out, not_166_out);
  nand nand_70 (nand_70_out, not_110_out, not_166_out);
  nand nand_71 (nand_71_out, not_111_out, not_125_out);
  nand nand_72 (nand_72_out, not_124_out, not_168_out);
  nand nand_73 (nand_73_out, not_111_out, not_168_out);
  nand nand_74 (nand_74_out, not_112_out, not_128_out);
  nand nand_75 (nand_75_out, not_127_out, not_170_out);
  nand nand_76 (nand_76_out, not_112_out, not_170_out);
  nand nand_77 (nand_77_out, not_113_out, not_131_out);
  nand nand_78 (nand_78_out, not_130_out, not_172_out);
  nand nand_79 (nand_79_out, not_113_out, not_172_out);
  nand nand_80 (nand_80_out, not_114_out, not_134_out);
  nand nand_81 (nand_81_out, not_133_out, not_174_out);
  nand nand_82 (nand_82_out, not_114_out, not_174_out);
  nand nand_83 (nand_83_out, not_115_out, not_137_out);
  nand nand_84 (nand_84_out, not_136_out, not_176_out);
  nand nand_85 (nand_85_out, not_115_out, not_176_out);
  nand nand_86 (nand_86_out, not_116_out, not_140_out);
  nand nand_87 (nand_87_out, not_139_out, not_178_out);
  nand nand_88 (nand_88_out, not_116_out, not_178_out);
  not not_141 (not_141_out, nand_65_out);
  not not_142 (not_142_out, nand_66_out);
  not not_143 (not_143_out, nand_67_out);
  not not_144 (not_144_out, nand_68_out);
  not not_145 (not_145_out, nand_69_out);
  not not_146 (not_146_out, nand_70_out);
  not not_147 (not_147_out, nand_71_out);
  not not_148 (not_148_out, nand_72_out);
  not not_149 (not_149_out, nand_73_out);
  not not_150 (not_150_out, nand_74_out);
  not not_151 (not_151_out, nand_75_out);
  not not_152 (not_152_out, nand_76_out);
  not not_153 (not_153_out, nand_77_out);
  not not_154 (not_154_out, nand_78_out);
  not not_155 (not_155_out, nand_79_out);
  not not_156 (not_156_out, nand_80_out);
  not not_157 (not_157_out, nand_81_out);
  not not_158 (not_158_out, nand_82_out);
  not not_159 (not_159_out, nand_83_out);
  not not_160 (not_160_out, nand_84_out);
  not not_161 (not_161_out, nand_85_out);
  not not_162 (not_162_out, nand_86_out);
  not not_163 (not_163_out, nand_87_out);
  not not_164 (not_164_out, nand_88_out);
  nor nor_25 (nor_25_out, not_141_out, not_142_out);
  nor nor_26 (nor_26_out, not_117_out, not_143_out);
  nor nor_27 (nor_27_out, not_144_out, not_145_out);
  nor nor_28 (nor_28_out, not_120_out, not_146_out);
  nor nor_29 (nor_29_out, not_147_out, not_148_out);
  nor nor_30 (nor_30_out, not_123_out, not_149_out);
  nor nor_31 (nor_31_out, not_150_out, not_151_out);
  nor nor_32 (nor_32_out, not_126_out, not_152_out);
  nor nor_33 (nor_33_out, not_153_out, not_154_out);
  nor nor_34 (nor_34_out, not_129_out, not_155_out);
  nor nor_35 (nor_35_out, not_156_out, not_157_out);
  nor nor_36 (nor_36_out, not_132_out, not_158_out);
  nor nor_37 (nor_37_out, not_159_out, not_160_out);
  nor nor_38 (nor_38_out, not_135_out, not_161_out);
  nor nor_39 (nor_39_out, not_162_out, not_163_out);
  nor nor_40 (nor_40_out, not_138_out, not_164_out);
  not not_165 (not_165_out, nor_25_out);
  not not_166 (not_166_out, nor_26_out);
  not not_167 (not_167_out, nor_27_out);
  not not_168 (not_168_out, nor_28_out);
  not not_169 (not_169_out, nor_29_out);
  not not_170 (not_170_out, nor_30_out);
  not not_171 (not_171_out, nor_31_out);
  not not_172 (not_172_out, nor_32_out);
  not not_173 (not_173_out, nor_33_out);
  not not_174 (not_174_out, nor_34_out);
  not not_175 (not_175_out, nor_35_out);
  not not_176 (not_176_out, nor_36_out);
  not not_177 (not_177_out, nor_37_out);
  not not_178 (not_178_out, nor_38_out);
  not not_179 (not_179_out, nor_39_out);
  not not_180 (out_31, nor_40_out);
  not not_181 (not_181_out, S_select);
  not not_182 (not_182_out, not_183_out);
  not not_183 (not_183_out, S_select);
  nand nand_89 (nand_89_out, not_165_out, S_select);
  nand nand_90 (nand_90_out, not_181_out, not_53_out);
  nand nand_91 (nand_91_out, not_165_out, not_53_out);
  nand nand_92 (nand_92_out, not_167_out, S_select);
  nand nand_93 (nand_93_out, not_181_out, not_54_out);
  nand nand_94 (nand_94_out, not_167_out, not_54_out);
  nand nand_95 (nand_95_out, not_169_out, S_select);
  nand nand_96 (nand_96_out, not_181_out, not_55_out);
  nand nand_97 (nand_97_out, not_169_out, not_55_out);
  nand nand_98 (nand_98_out, not_171_out, S_select);
  nand nand_99 (nand_99_out, not_181_out, not_56_out);
  nand nand_100 (nand_100_out, not_171_out, not_56_out);
  nand nand_101 (nand_101_out, not_173_out, S_select);
  nand nand_102 (nand_102_out, not_181_out, not_57_out);
  nand nand_103 (nand_103_out, not_173_out, not_57_out);
  nand nand_104 (nand_104_out, not_175_out, S_select);
  nand nand_105 (nand_105_out, not_181_out, not_58_out);
  nand nand_106 (nand_106_out, not_175_out, not_58_out);
  nand nand_107 (nand_107_out, not_177_out, S_select);
  nand nand_108 (nand_108_out, not_181_out, not_59_out);
  nand nand_109 (nand_109_out, not_177_out, not_59_out);
  nand nand_110 (nand_110_out, not_179_out, S_select);
  nand nand_111 (nand_111_out, not_181_out, not_60_out);
  nand nand_112 (nand_112_out, not_179_out, not_60_out);
  nand nand_113 (nand_113_out, not_61_out, not_183_out);
  nand nand_114 (nand_114_out, not_182_out, not_101_out);
  nand nand_115 (nand_115_out, not_61_out, not_101_out);
  nand nand_116 (nand_116_out, not_62_out, not_183_out);
  nand nand_117 (nand_117_out, not_182_out, not_102_out);
  nand nand_118 (nand_118_out, not_62_out, not_102_out);
  nand nand_119 (nand_119_out, not_63_out, not_183_out);
  nand nand_120 (nand_120_out, not_182_out, not_103_out);
  nand nand_121 (nand_121_out, not_63_out, not_103_out);
  nand nand_122 (nand_122_out, not_64_out, not_183_out);
  nand nand_123 (nand_123_out, not_182_out, not_104_out);
  nand nand_124 (nand_124_out, not_64_out, not_104_out);
  nand nand_125 (nand_125_out, not_65_out, not_183_out);
  nand nand_126 (nand_126_out, not_182_out, not_105_out);
  nand nand_127 (nand_127_out, not_65_out, not_105_out);
  nand nand_128 (nand_128_out, not_66_out, not_183_out);
  nand nand_129 (nand_129_out, not_182_out, not_106_out);
  nand nand_130 (nand_130_out, not_66_out, not_106_out);
  nand nand_131 (nand_131_out, not_67_out, not_183_out);
  nand nand_132 (nand_132_out, not_182_out, not_107_out);
  nand nand_133 (nand_133_out, not_67_out, not_107_out);
  nand nand_134 (nand_134_out, not_68_out, not_183_out);
  nand nand_135 (nand_135_out, not_182_out, not_108_out);
  nand nand_136 (nand_136_out, not_68_out, not_108_out);
  not not_184 (not_184_out, nand_89_out);
  not not_185 (not_185_out, nand_90_out);
  not not_186 (not_186_out, nand_91_out);
  not not_187 (not_187_out, nand_92_out);
  not not_188 (not_188_out, nand_93_out);
  not not_189 (not_189_out, nand_94_out);
  not not_190 (not_190_out, nand_95_out);
  not not_191 (not_191_out, nand_96_out);
  not not_192 (not_192_out, nand_97_out);
  not not_193 (not_193_out, nand_98_out);
  not not_194 (not_194_out, nand_99_out);
  not not_195 (not_195_out, nand_100_out);
  not not_196 (not_196_out, nand_101_out);
  not not_197 (not_197_out, nand_102_out);
  not not_198 (not_198_out, nand_103_out);
  not not_199 (not_199_out, nand_104_out);
  not not_200 (not_200_out, nand_105_out);
  not not_201 (not_201_out, nand_106_out);
  not not_202 (not_202_out, nand_107_out);
  not not_203 (not_203_out, nand_108_out);
  not not_204 (not_204_out, nand_109_out);
  not not_205 (not_205_out, nand_110_out);
  not not_206 (not_206_out, nand_111_out);
  not not_207 (not_207_out, nand_112_out);
  not not_208 (not_208_out, nand_113_out);
  not not_209 (not_209_out, nand_114_out);
  not not_210 (not_210_out, nand_115_out);
  not not_211 (not_211_out, nand_116_out);
  not not_212 (not_212_out, nand_117_out);
  not not_213 (not_213_out, nand_118_out);
  not not_214 (not_214_out, nand_119_out);
  not not_215 (not_215_out, nand_120_out);
  not not_216 (not_216_out, nand_121_out);
  not not_217 (not_217_out, nand_122_out);
  not not_218 (not_218_out, nand_123_out);
  not not_219 (not_219_out, nand_124_out);
  not not_220 (not_220_out, nand_125_out);
  not not_221 (not_221_out, nand_126_out);
  not not_222 (not_222_out, nand_127_out);
  not not_223 (not_223_out, nand_128_out);
  not not_224 (not_224_out, nand_129_out);
  not not_225 (not_225_out, nand_130_out);
  not not_226 (not_226_out, nand_131_out);
  not not_227 (not_227_out, nand_132_out);
  not not_228 (not_228_out, nand_133_out);
  not not_229 (not_229_out, nand_134_out);
  not not_230 (not_230_out, nand_135_out);
  not not_231 (not_231_out, nand_136_out);
  nor nor_41 (nor_41_out, not_184_out, not_185_out, not_186_out);
  nor nor_42 (nor_42_out, not_187_out, not_188_out, not_189_out);
  nor nor_43 (nor_43_out, not_190_out, not_191_out, not_192_out);
  nor nor_44 (nor_44_out, not_193_out, not_194_out, not_195_out);
  nor nor_45 (nor_45_out, not_196_out, not_197_out, not_198_out);
  nor nor_46 (nor_46_out, not_199_out, not_200_out, not_201_out);
  nor nor_47 (nor_47_out, not_202_out, not_203_out, not_204_out);
  nor nor_48 (nor_48_out, not_205_out, not_206_out, not_207_out);
  nor nor_49 (nor_49_out, not_208_out, not_209_out, not_210_out);
  nor nor_50 (nor_50_out, not_211_out, not_212_out, not_213_out);
  nor nor_51 (nor_51_out, not_214_out, not_215_out, not_216_out);
  nor nor_52 (nor_52_out, not_217_out, not_218_out, not_219_out);
  nor nor_53 (nor_53_out, not_220_out, not_221_out, not_222_out);
  nor nor_54 (nor_54_out, not_223_out, not_224_out, not_225_out);
  nor nor_55 (nor_55_out, not_226_out, not_227_out, not_228_out);
  nor nor_56 (nor_56_out, not_229_out, not_230_out, not_231_out);
  not not_232 (not_232_out, nor_41_out);
  not not_233 (not_233_out, nor_42_out);
  not not_234 (not_234_out, nor_43_out);
  not not_235 (not_235_out, nor_44_out);
  not not_236 (not_236_out, nor_45_out);
  not not_237 (not_237_out, nor_46_out);
  not not_238 (not_238_out, nor_47_out);
  not not_239 (not_239_out, nor_48_out);
  not not_240 (not_240_out, nor_49_out);
  not not_241 (not_241_out, nor_50_out);
  not not_242 (not_242_out, nor_51_out);
  not not_243 (not_243_out, nor_52_out);
  not not_244 (not_244_out, nor_53_out);
  not not_245 (not_245_out, nor_54_out);
  not not_246 (not_246_out, nor_55_out);
  not not_247 (not_247_out, nor_56_out);
  not not_248 (not_248_out, S_select_2);
  nand nand_137 (nand_137_out, not_232_out, S_select_2);
  nand nand_138 (nand_138_out, not_248_out, not_240_out);
  nand nand_139 (nand_139_out, not_232_out, not_240_out);
  nand nand_140 (nand_140_out, not_233_out, S_select_2);
  nand nand_141 (nand_141_out, not_248_out, not_241_out);
  nand nand_142 (nand_142_out, not_233_out, not_241_out);
  nand nand_143 (nand_143_out, not_234_out, S_select_2);
  nand nand_144 (nand_144_out, not_248_out, not_242_out);
  nand nand_145 (nand_145_out, not_234_out, not_242_out);
  nand nand_146 (nand_146_out, not_235_out, S_select_2);
  nand nand_147 (nand_147_out, not_248_out, not_243_out);
  nand nand_148 (nand_148_out, not_235_out, not_243_out);
  nand nand_149 (nand_149_out, not_236_out, S_select_2);
  nand nand_150 (nand_150_out, not_248_out, not_244_out);
  nand nand_151 (nand_151_out, not_236_out, not_244_out);
  nand nand_152 (nand_152_out, not_237_out, S_select_2);
  nand nand_153 (nand_153_out, not_248_out, not_245_out);
  nand nand_154 (nand_154_out, not_237_out, not_245_out);
  nand nand_155 (nand_155_out, not_238_out, S_select_2);
  nand nand_156 (nand_156_out, not_248_out, not_246_out);
  nand nand_157 (nand_157_out, not_238_out, not_246_out);
  nand nand_158 (nand_158_out, not_239_out, S_select_2);
  nand nand_159 (nand_159_out, not_248_out, not_247_out);
  nand nand_160 (nand_160_out, not_239_out, not_247_out);
  not not_249 (not_249_out, nand_137_out);
  not not_250 (not_250_out, nand_138_out);
  not not_251 (not_251_out, nand_139_out);
  not not_252 (not_252_out, nand_140_out);
  not not_253 (not_253_out, nand_141_out);
  not not_254 (not_254_out, nand_142_out);
  not not_255 (not_255_out, nand_143_out);
  not not_256 (not_256_out, nand_144_out);
  not not_257 (not_257_out, nand_145_out);
  not not_258 (not_258_out, nand_146_out);
  not not_259 (not_259_out, nand_147_out);
  not not_260 (not_260_out, nand_148_out);
  not not_261 (not_261_out, nand_149_out);
  not not_262 (not_262_out, nand_150_out);
  not not_263 (not_263_out, nand_151_out);
  not not_264 (not_264_out, nand_152_out);
  not not_265 (not_265_out, nand_153_out);
  not not_266 (not_266_out, nand_154_out);
  not not_267 (not_267_out, nand_155_out);
  not not_268 (not_268_out, nand_156_out);
  not not_269 (not_269_out, nand_157_out);
  not not_270 (not_270_out, nand_158_out);
  not not_271 (not_271_out, nand_159_out);
  not not_272 (not_272_out, nand_160_out);
  nor nor_57 (nor_57_out, not_249_out, not_250_out, not_251_out);
  nor nor_58 (nor_58_out, not_252_out, not_253_out, not_254_out);
  nor nor_59 (nor_59_out, not_255_out, not_256_out, not_257_out);
  nor nor_60 (nor_60_out, not_258_out, not_259_out, not_260_out);
  nor nor_61 (nor_61_out, not_261_out, not_262_out, not_263_out);
  nor nor_62 (nor_62_out, not_264_out, not_265_out, not_266_out);
  nor nor_63 (nor_63_out, not_267_out, not_268_out, not_269_out);
  nor nor_64 (nor_64_out, not_270_out, not_271_out, not_272_out);
  not not_273 (OUT16, nor_57_out);
  not not_274 (OUT17, nor_58_out);
  not not_275 (OUT18, nor_59_out);
  not not_276 (OUT19, nor_60_out);
  not not_277 (OUT20, nor_61_out);
  not not_278 (OUT21, nor_62_out);
  not not_279 (OUT22, nor_63_out);
  not not_280 (OUT23, nor_64_out);

  // Notes on the sheet:
  //   _15_alu: DEL
  //   _14_alu: DEL
  //   _13_alu: DEL
  //   _12_alu: DEL
  //   _11_alu: DEL
  //   _10_alu: DEL
  //   _9_alu: DEL
  //   _8_alu: DEL
  //   _7_alu: CMP
  //   _6_alu: SHR
  //   _5_alu: SHL
  //   _4_alu: XOR
  //   _3_alu: OR
  //   _2_alu: AND
  //   _1_sub: SUB
  //   _0_alu: ADD
  //   0-phase
  //   1-phase
endmodule
