// Digital circuit ANY register apt wth driver.dig as structural Verilog
module ANY_register_apt_wth_driver (
  input  Data4,
  input  Data5,
  input  Data6,
  input  Data7,
  input  Data0,
  input  Data1,
  input  Data2,
  input  Data3,
  input  CLK,
  input  Reset,
  input  OE,
  output Q4,
  output Q5,
  output Q6,
  output Q7,
  output Q0,
  output Q1,
  output Q2,
  output Q3,
  output Q0_2,
  output Q1_2,
  output Q2_2,
  output Q3_2,
  output Q4_2,
  output Q5_2,
  output Q6_2,
  output Q7_2
);

  wire nand_1_out, nand_2_out, nand_3_out, nand_4_out, nand_5_out, nand_6_out, nand_7_out, nand_8_out,
       nand_9_out, nand_10_out, nand_11_out, nand_12_out, nand_13_out, nand_14_out, nand_15_out, nand_16_out,
       nand_17_out, nand_19_out, nand_21_out, nand_23_out, nand_25_out, nand_27_out, nand_29_out,
       nand_31_out, not_1_out, not_2_out, not_3_out, not_4_out, not_5_out, not_6_out, not_7_out, not_8_out,
       not_9_out;

  not not_1 (not_1_out, Reset);
  not not_2 (not_2_out, Data0);
  not not_3 (not_3_out, Data1);
  not not_4 (not_4_out, Data2);
  not not_5 (not_5_out, Data3);
  not not_6 (not_6_out, Data4);
  not not_7 (not_7_out, Data5);
  not not_8 (not_8_out, Data6);
  not not_9 (not_9_out, Data7);
  nand nand_1 (nand_1_out, Data0, not_1_out, CLK);
  nand nand_2 (nand_2_out, not_2_out, CLK);
  nand nand_3 (nand_3_out, Data1, not_1_out, CLK);
  nand nand_4 (nand_4_out, not_3_out, CLK);
  nand nand_5 (nand_5_out, Data2, not_1_out, CLK);
  nand nand_6 (nand_6_out, not_4_out, CLK);
  nand nand_7 (nand_7_out, Data3, not_1_out, CLK);
  nand nand_8 (nand_8_out, not_5_out, CLK);
  nand nand_9 (nand_9_out, Data4, not_1_out, CLK);
  nand nand_10 (nand_10_out, not_6_out, CLK);
  nand nand_11 (nand_11_out, Data5, not_1_out, CLK);
  nand nand_12 (nand_12_out, not_7_out, CLK);
  nand nand_13 (nand_13_out, Data6, not_1_out, CLK);
  nand nand_14 (nand_14_out, not_8_out, CLK);
  nand nand_15 (nand_15_out, Data7, not_1_out, CLK);
  nand nand_16 (nand_16_out, not_9_out, CLK);
  nand nand_17 (nand_17_out, nand_1_out, Q0);
  nand nand_18 (Q0, nand_17_out, nand_2_out);
  nand nand_19 (nand_19_out, nand_3_out, Q1);
  nand nand_20 (Q1, nand_19_out, nand_4_out);
  nand nand_21 (nand_21_out, nand_5_out, Q2);
  nand nand_22 (Q2, nand_21_out, nand_6_out);
  nand nand_23 (nand_23_out, nand_7_out, Q3);
  nand nand_24 (Q3, nand_23_out, nand_8_out);
  nand nand_25 (nand_25_out, nand_9_out, Q4);
  nand nand_26 (Q4, nand_25_out, nand_10_out);
  nand nand_27 (nand_27_out, nand_11_out, Q5);
  nand nand_28 (Q5, nand_27_out, nand_12_out);
  nand nand_29 (nand_29_out, nand_13_out, Q6);
  nand nand_30 (Q6, nand_29_out, nand_14_out);
  nand nand_31 (nand_31_out, nand_15_out, Q7);
  nand nand_32 (Q7, nand_31_out, nand_16_out);
  assign Q0_2 = OE ? nand_17_out : 1'bz;  // Driver driver_1
  assign Q1_2 = OE ? nand_19_out : 1'bz;  // Driver driver_2
  assign Q2_2 = OE ? nand_21_out : 1'bz;  // Driver driver_3
  assign Q3_2 = OE ? nand_23_out : 1'bz;  // Driver driver_4
  assign Q4_2 = OE ? nand_25_out : 1'bz;  // Driver driver_5
  assign Q5_2 = OE ? nand_27_out : 1'bz;  // Driver driver_6
  assign Q6_2 = OE ? nand_29_out : 1'bz;  // Driver driver_7
  assign Q7_2 = OE ? nand_31_out : 1'bz;  // Driver driver_8
endmodule
