// Digital circuit D-trigger wth gen.dig as structural Verilog
module D_trigger_wth_gen (
  input  Data,
  input  clk,
  output Q,
  output Q_2
);

  wire nand_1_out, nand_2_out, not_1_out;

  not not_1 (not_1_out, Data);
  nand nand_1 (nand_1_out, Data, clk);
  nand nand_2 (nand_2_out, not_1_out, clk);
  nand nand_3 (Q, nand_1_out, Q_2);
  nand nand_4 (Q_2, Q, nand_2_out);
endmodule
