// Digital circuit D-trigger.dig as structural Verilog
module D_trigger (
  input  Data,
  input  CLK,
  input  Data_2,
  input  CLK_2,
  output Q,
  output Q_2,
  output Q_3,
  output Q_4
);

  wire nand_1_out, nand_2_out, nand_3_out, nand_4_out, not_1_out, not_2_out, undriven;

  not not_1 (not_1_out, Data_2);
  not not_2 (not_2_out, Data);
  nand nand_1 (nand_1_out, not_1_out, undriven);
  nand nand_2 (nand_2_out, undriven, CLK_2);
  nand nand_3 (nand_3_out, Data, CLK);
  nand nand_4 (nand_4_out, not_2_out, CLK);
  nand nand_5 (Q_3, nand_1_out, Q_4);
  nand nand_6 (Q_4, Q_3, nand_2_out);
  nand nand_7 (Q, nand_3_out, Q_2);
  nand nand_8 (Q_2, Q, nand_4_out);
endmodule
