// Digital circuit Decoder_16_alu.dig as structural Verilog
module Decoder_16_alu (
  input  INP3,
  input  INP2,
  input  INP1,
  input  INP0,
  output _15_alu,
  output _14_alu,
  output _13_alu,
  output _12_alu,
  output _11_alu,
  output _10_alu,
  output _9_alu,
  output _8_alu,
  output _7_alu,
  output _6_alu,
  output _5_alu,
  output _4_alu,
  output _3_alu,
  output _2_alu,
  output _1_sub,
  output _0_alu
);

  wire nand_1_out, nand_2_out, nand_3_out, nand_4_out, nand_5_out, nand_6_out, nand_7_out, nand_8_out,
       nand_9_out, nand_10_out, nand_11_out, nand_12_out, nand_13_out, nand_14_out, nand_15_out, nand_16_out,
       not_2_out, not_8_out, not_13_out, not_20_out;

  not not_1 (_15_alu, nand_1_out);
  not not_2 (not_2_out, INP3);
  nand nand_1 (nand_1_out, INP0, INP1, INP2, INP3);
  nand nand_2 (nand_2_out, not_20_out, INP1, INP2, INP3);
  not not_3 (_14_alu, nand_2_out);
  not not_4 (_13_alu, nand_3_out);
  nand nand_3 (nand_3_out, INP0, not_13_out, INP2, INP3);
  nand nand_4 (nand_4_out, not_20_out, not_13_out, INP2, INP3);
  not not_5 (_12_alu, nand_4_out);
  not not_6 (_11_alu, nand_5_out);
  nand nand_5 (nand_5_out, INP0, INP1, not_8_out, INP3);
  nand nand_6 (nand_6_out, not_20_out, INP1, not_8_out, INP3);
  not not_7 (_10_alu, nand_6_out);
  not not_8 (not_8_out, INP2);
  not not_9 (_9_alu, nand_7_out);
  nand nand_7 (nand_7_out, INP0, not_13_out, not_8_out, INP3);
  nand nand_8 (nand_8_out, not_20_out, not_13_out, not_8_out, INP3);
  not not_10 (_8_alu, nand_8_out);
  nand nand_9 (nand_9_out, INP0, INP1, INP2, not_2_out);
  not not_11 (_7_alu, nand_9_out);
  not not_12 (_6_alu, nand_10_out);
  nand nand_10 (nand_10_out, not_20_out, INP1, INP2, not_2_out);
  not not_13 (not_13_out, INP1);
  nand nand_11 (nand_11_out, INP0, not_13_out, INP2, not_2_out);
  not not_14 (_5_alu, nand_11_out);
  not not_15 (_4_alu, nand_12_out);
  nand nand_12 (nand_12_out, not_20_out, not_13_out, INP2, not_2_out);
  nand nand_13 (nand_13_out, INP0, INP1, not_8_out, not_2_out);
  not not_16 (_3_alu, nand_13_out);
  not not_17 (_2_alu, nand_14_out);
  nand nand_14 (nand_14_out, not_20_out, INP1, not_8_out, not_2_out);
  nand nand_15 (nand_15_out, INP0, not_13_out, not_8_out, not_2_out);
  not not_18 (_1_sub, nand_15_out);
  not not_19 (_0_alu, nand_16_out);
  not not_20 (not_20_out, INP0);
  nand nand_16 (nand_16_out, not_20_out, not_13_out, not_8_out, not_2_out);

  // Notes on the sheet:
  //   _15_alu: DEL
  //   _14_alu: DEL
  //   _13_alu: DEL
  //   _12_alu: DEL
  //   _11_alu: DEL
  //   _10_alu: DEL
  //   _9_alu: DEL
  //   _8_alu: DEL
  //   _7_alu: CMP
  //   _6_alu: SHR
  //   _5_alu: SHL
  //   _4_alu: XOR
  //   _3_alu: OR
  //   _2_alu: AND
  //   _1_sub: SUB
  //   _0_alu: ADD
  //   0-phase
  //   1-phase
endmodule
