// Digital circuit Decoder_16_com.dig as structural Verilog
module Decoder_16_com (
  input  INP3,
  input  INP2,
  input  INP1,
  input  INP0,
  output _15_com,
  output _14_com,
  output _13_com,
  output _12_com,
  output _11_com,
  output _10_com,
  output _9_com,
  output _8_com,
  output _7_com,
  output _6_com,
  output _5_com,
  output _4_com,
  output _3_com,
  output _2_com,
  output _1_com,
  output _0_com
);

  wire nand_1_out, nand_2_out, nand_3_out, nand_4_out, nand_5_out, nand_6_out, nand_7_out, nand_8_out,
       nand_9_out, nand_10_out, nand_11_out, nand_12_out, nand_13_out, nand_14_out, nand_15_out, nand_16_out,
       not_2_out, not_8_out, not_13_out, not_20_out;

  not not_1 (_15_com, nand_1_out);
  not not_2 (not_2_out, INP3);
  nand nand_1 (nand_1_out, INP0, INP1, INP2, INP3);
  nand nand_2 (nand_2_out, not_20_out, INP1, INP2, INP3);
  not not_3 (_14_com, nand_2_out);
  not not_4 (_13_com, nand_3_out);
  nand nand_3 (nand_3_out, INP0, not_13_out, INP2, INP3);
  nand nand_4 (nand_4_out, not_20_out, not_13_out, INP2, INP3);
  not not_5 (_12_com, nand_4_out);
  not not_6 (_11_com, nand_5_out);
  nand nand_5 (nand_5_out, INP0, INP1, not_8_out, INP3);
  nand nand_6 (nand_6_out, not_20_out, INP1, not_8_out, INP3);
  not not_7 (_10_com, nand_6_out);
  not not_8 (not_8_out, INP2);
  not not_9 (_9_com, nand_7_out);
  nand nand_7 (nand_7_out, INP0, not_13_out, not_8_out, INP3);
  nand nand_8 (nand_8_out, not_20_out, not_13_out, not_8_out, INP3);
  not not_10 (_8_com, nand_8_out);
  nand nand_9 (nand_9_out, INP0, INP1, INP2, not_2_out);
  not not_11 (_7_com, nand_9_out);
  not not_12 (_6_com, nand_10_out);
  nand nand_10 (nand_10_out, not_20_out, INP1, INP2, not_2_out);
  not not_13 (not_13_out, INP1);
  nand nand_11 (nand_11_out, INP0, not_13_out, INP2, not_2_out);
  not not_14 (_5_com, nand_11_out);
  not not_15 (_4_com, nand_12_out);
  nand nand_12 (nand_12_out, not_20_out, not_13_out, INP2, not_2_out);
  nand nand_13 (nand_13_out, INP0, INP1, not_8_out, not_2_out);
  not not_16 (_3_com, nand_13_out);
  not not_17 (_2_com, nand_14_out);
  nand nand_14 (nand_14_out, not_20_out, INP1, not_8_out, not_2_out);
  nand nand_15 (nand_15_out, INP0, not_13_out, not_8_out, not_2_out);
  not not_18 (_1_com, nand_15_out);
  not not_19 (_0_com, nand_16_out);
  not not_20 (not_20_out, INP0);
  nand nand_16 (nand_16_out, not_20_out, not_13_out, not_8_out, not_2_out);

  // Notes on the sheet:
  //   _15_com: HLT (Halt)
  //   _14_com: LDI BX, Value (Load Immediate)
  //   _13_com: LDI AX, Value (Load Immediate)
  //   _12_com: OUT [Port], AX (Output AX on interface)
  //   _11_com: JNZ [Addr] (Jump if Not Zero)
  //   _10_com: JZ [Addr] (Jump if Zero)
  //   _9_com: JMP [Addr] (Jump)
  //   _8_com: SUB AX, BX (Subtract AX and BX res AX)
  //   _7_com: ADD AX, BX (Add AX and BX res AX)
  //   _6_com: MOV BX, AX (Copy AX in BX)
  //   _5_com: MOV AX, BX (Copy BX in AX)
  //   _4_com: STA BX, [Addr] (Store BX)
  //   _3_com: STA AX, [Addr] (Store AX)
  //   _2_com: LDA BX, [Addr] (Load BX)
  //   _1_com: LDA AX, [Addr] (Load AX)
  //   _0_com: NOP(No Operation)
  //   0-phase
  //   1-phase
endmodule
