// Digital circuit Decoder_16_reg.dig as structural Verilog
module Decoder_16_reg (
  input  INP3,
  input  INP2,
  input  INP1,
  input  INP0,
  output _15_reg,
  output _14_reg,
  output _13_reg,
  output _12_reg,
  output _11_reg,
  output _10_reg,
  output _9_reg,
  output _8_reg,
  output _7_reg,
  output _6_reg,
  output _5_reg,
  output _4_reg,
  output _3_reg,
  output _2_reg,
  output _1_reg,
  output _0_reg
);

  wire nand_1_out, nand_2_out, nand_3_out, nand_4_out, nand_5_out, nand_6_out, nand_7_out, nand_8_out,
       nand_9_out, nand_10_out, nand_11_out, nand_12_out, nand_13_out, nand_14_out, nand_15_out, nand_16_out,
       not_2_out, not_8_out, not_14_out, not_19_out;

  nand nand_1 (nand_1_out, INP0, INP1, INP2, INP3);
  not not_1 (_15_reg, nand_1_out);
  not not_2 (not_2_out, INP3);
  not not_3 (_14_reg, nand_2_out);
  nand nand_2 (nand_2_out, not_19_out, INP1, INP2, INP3);
  nand nand_3 (nand_3_out, INP0, not_14_out, INP2, INP3);
  not not_4 (_13_reg, nand_3_out);
  not not_5 (_12_reg, nand_4_out);
  nand nand_4 (nand_4_out, not_19_out, not_14_out, INP2, INP3);
  nand nand_5 (nand_5_out, INP0, INP1, not_8_out, INP3);
  not not_6 (_11_reg, nand_5_out);
  not not_7 (_10_reg, nand_6_out);
  not not_8 (not_8_out, INP2);
  nand nand_6 (nand_6_out, not_19_out, INP1, not_8_out, INP3);
  nand nand_7 (nand_7_out, INP0, not_14_out, not_8_out, INP3);
  not not_9 (_9_reg, nand_7_out);
  not not_10 (_8_reg, nand_8_out);
  nand nand_8 (nand_8_out, not_19_out, not_14_out, not_8_out, INP3);
  not not_11 (_7_reg, nand_9_out);
  nand nand_9 (nand_9_out, INP0, INP1, INP2, not_2_out);
  nand nand_10 (nand_10_out, not_19_out, INP1, INP2, not_2_out);
  not not_12 (_6_reg, nand_10_out);
  not not_13 (_5_reg, nand_11_out);
  not not_14 (not_14_out, INP1);
  nand nand_11 (nand_11_out, INP0, not_14_out, INP2, not_2_out);
  nand nand_12 (nand_12_out, not_19_out, not_14_out, INP2, not_2_out);
  not not_15 (_4_reg, nand_12_out);
  not not_16 (_3_reg, nand_13_out);
  nand nand_13 (nand_13_out, INP0, INP1, not_8_out, not_2_out);
  nand nand_14 (nand_14_out, not_19_out, INP1, not_8_out, not_2_out);
  not not_17 (_2_reg, nand_14_out);
  not not_18 (_1_reg, nand_15_out);
  nand nand_15 (nand_15_out, INP0, not_14_out, not_8_out, not_2_out);
  not not_19 (not_19_out, INP0);
  nand nand_16 (nand_16_out, not_19_out, not_14_out, not_8_out, not_2_out);
  not not_20 (_0_reg, nand_16_out);

  // Notes on the sheet:
  //   _15_reg: FREE
  //   _14_reg: OF(Overflow Flag)
  //   _13_reg: CF(Carry Flag)
  //   _12_reg: ZF(Zero Flag)
  //   _11_reg: ZERO(mask of 0, ground)
  //   _10_reg: ONES(mask of 1)
  //   _9_reg: MDR(Memory Data Register)
  //   _8_reg: MAR(Memory Adress Register)
  //   _7_reg: FREE
  //   _6_reg: SP(Stack Pointer)
  //   _5_reg: FREE
  //   _4_reg: IP(Instruction Pointer)
  //   _3_reg: DX(Data)
  //   _2_reg: CX(Counter)
  //   _1_reg: BX(Base)
  //   _0_reg: AX(Accumulator)
  //   0-phase
  //   1-phase
endmodule
