// Digital circuit Full Adder_1b.dig as structural Verilog
module Full_Adder_1b (
  input  A,
  input  B,
  input  C_in,
  output Sum,
  output C_out
);

  wire nand_1_out, nand_2_out, nand_3_out, nand_4_out, nand_5_out, nand_6_out, nor_1_out, nor_2_out,
       nor_3_out, not_1_out, not_2_out, not_3_out, not_4_out, not_5_out, not_6_out, not_7_out, not_8_out,
       not_9_out, not_10_out, not_11_out;

  not not_1 (not_1_out, A);
  not not_2 (not_2_out, B);
  nand nand_1 (nand_1_out, A, B);
  nand nand_2 (nand_2_out, A, not_2_out);
  nand nand_3 (nand_3_out, not_1_out, B);
  not not_3 (not_3_out, nand_2_out);
  not not_4 (not_4_out, nand_3_out);
  nor nor_1 (nor_1_out, not_3_out, not_4_out);
  not not_5 (not_5_out, nor_1_out);
  not not_6 (not_6_out, nand_1_out);
  not not_7 (not_7_out, not_5_out);
  not not_8 (not_8_out, C_in);
  nand nand_4 (nand_4_out, not_5_out, not_8_out);
  nand nand_5 (nand_5_out, not_7_out, C_in);
  nand nand_6 (nand_6_out, not_5_out, C_in);
  not not_9 (not_9_out, nand_4_out);
  not not_10 (not_10_out, nand_5_out);
  not not_11 (not_11_out, nand_6_out);
  nor nor_2 (nor_2_out, not_9_out, not_10_out);
  nor nor_3 (nor_3_out, not_6_out, not_11_out);
  not not_12 (Sum, nor_2_out);
  not not_13 (C_out, nor_3_out);
endmodule
