// Digital circuit Full Adder_8b.dig as structural Verilog
module Full_Adder_8b (
  input  A0,
  input  B0,
  input  A1,
  input  B1,
  input  A2,
  input  B2,
  input  A3,
  input  B3,
  input  A4,
  input  B4,
  input  A5,
  input  B5,
  input  A6,
  input  B6,
  input  A7,
  input  B7,
  output Sum0,
  output Sum1,
  output Sum2,
  output Sum3,
  output Sum4,
  output Sum5,
  output Sum6,
  output Sum7,
  output C_out7
);

  wire nand_1_out, nand_2_out, nand_3_out, nand_4_out, nand_5_out, nand_6_out, nand_7_out, nand_8_out,
       nand_9_out, nand_10_out, nand_11_out, nand_12_out, nand_13_out, nand_14_out, nand_15_out, nand_16_out,
       nand_17_out, nand_18_out, nand_19_out, nand_20_out, nand_21_out, nand_22_out, nand_23_out,
       nand_24_out, nand_25_out, nand_26_out, nand_27_out, nand_28_out, nand_29_out, nand_30_out,
       nand_31_out, nand_32_out, nand_33_out, nand_34_out, nand_35_out, nand_36_out, nand_37_out,
       nand_38_out, nand_39_out, nand_40_out, nand_41_out, nand_42_out, nand_43_out, nand_44_out,
       nand_45_out, nand_46_out, nand_47_out, nand_48_out, nor_1_out, nor_2_out, nor_3_out, nor_4_out,
       nor_5_out, nor_6_out, nor_7_out, nor_8_out, nor_9_out, nor_10_out, nor_11_out, nor_12_out, nor_13_out,
       nor_14_out, nor_15_out, nor_16_out, nor_17_out, nor_18_out, nor_19_out, nor_20_out, nor_21_out,
       nor_22_out, nor_23_out, nor_24_out, not_1_out, not_2_out, not_3_out, not_4_out, not_5_out, not_6_out,
       not_7_out, not_8_out, not_9_out, not_10_out, not_11_out, not_12_out, not_13_out, not_14_out,
       not_15_out, not_16_out, not_17_out, not_18_out, not_19_out, not_20_out, not_21_out, not_22_out,
       not_23_out, not_24_out, not_25_out, not_26_out, not_27_out, not_28_out, not_29_out, not_30_out,
       not_31_out, not_32_out, not_33_out, not_34_out, not_35_out, not_36_out, not_37_out, not_38_out,
       not_39_out, not_40_out, not_41_out, not_42_out, not_43_out, not_44_out, not_45_out, not_46_out,
       not_47_out, not_48_out, not_49_out, not_50_out, not_51_out, not_52_out, not_53_out, not_54_out,
       not_55_out, not_56_out, not_57_out, not_58_out, not_59_out, not_60_out, not_61_out, not_62_out,
       not_63_out, not_64_out, not_65_out, not_66_out, not_67_out, not_68_out, not_69_out, not_70_out,
       not_71_out, not_72_out, not_73_out, not_74_out, not_75_out, not_76_out, not_77_out, not_78_out,
       not_79_out, not_80_out, not_81_out, not_82_out, not_83_out, not_84_out, not_85_out, not_86_out,
       not_87_out, not_88_out, not_90_out, not_92_out, not_94_out, not_96_out, not_98_out, not_100_out,
       not_102_out;

  not not_1 (not_1_out, A0);
  not not_2 (not_2_out, B0);
  not not_3 (not_3_out, A1);
  not not_4 (not_4_out, B1);
  not not_5 (not_5_out, A2);
  not not_6 (not_6_out, B2);
  not not_7 (not_7_out, A3);
  not not_8 (not_8_out, B3);
  not not_9 (not_9_out, A4);
  not not_10 (not_10_out, B4);
  not not_11 (not_11_out, A5);
  not not_12 (not_12_out, B5);
  not not_13 (not_13_out, A6);
  not not_14 (not_14_out, B6);
  not not_15 (not_15_out, A7);
  not not_16 (not_16_out, B7);
  nand nand_1 (nand_1_out, A0, B0);
  nand nand_2 (nand_2_out, A0, not_2_out);
  nand nand_3 (nand_3_out, not_1_out, B0);
  nand nand_4 (nand_4_out, A1, B1);
  nand nand_5 (nand_5_out, A1, not_4_out);
  nand nand_6 (nand_6_out, not_3_out, B1);
  nand nand_7 (nand_7_out, A2, B2);
  nand nand_8 (nand_8_out, A2, not_6_out);
  nand nand_9 (nand_9_out, not_5_out, B2);
  nand nand_10 (nand_10_out, A3, B3);
  nand nand_11 (nand_11_out, A3, not_8_out);
  nand nand_12 (nand_12_out, not_7_out, B3);
  nand nand_13 (nand_13_out, A4, B4);
  nand nand_14 (nand_14_out, A4, not_10_out);
  nand nand_15 (nand_15_out, not_9_out, B4);
  nand nand_16 (nand_16_out, A5, B5);
  nand nand_17 (nand_17_out, A5, not_12_out);
  nand nand_18 (nand_18_out, not_11_out, B5);
  nand nand_19 (nand_19_out, A6, B6);
  nand nand_20 (nand_20_out, A6, not_14_out);
  nand nand_21 (nand_21_out, not_13_out, B6);
  nand nand_22 (nand_22_out, A7, B7);
  nand nand_23 (nand_23_out, A7, not_16_out);
  nand nand_24 (nand_24_out, not_15_out, B7);
  not not_17 (not_17_out, nand_2_out);
  nor nor_1 (nor_1_out, not_17_out, not_18_out);
  not not_18 (not_18_out, nand_3_out);
  not not_19 (not_19_out, nand_5_out);
  nor nor_2 (nor_2_out, not_19_out, not_20_out);
  not not_20 (not_20_out, nand_6_out);
  not not_21 (not_21_out, nand_8_out);
  nor nor_3 (nor_3_out, not_21_out, not_22_out);
  not not_22 (not_22_out, nand_9_out);
  not not_23 (not_23_out, nand_11_out);
  nor nor_4 (nor_4_out, not_23_out, not_24_out);
  not not_24 (not_24_out, nand_12_out);
  not not_25 (not_25_out, nand_14_out);
  nor nor_5 (nor_5_out, not_25_out, not_26_out);
  not not_26 (not_26_out, nand_15_out);
  not not_27 (not_27_out, nand_17_out);
  nor nor_6 (nor_6_out, not_27_out, not_28_out);
  not not_28 (not_28_out, nand_18_out);
  not not_29 (not_29_out, nand_20_out);
  nor nor_7 (nor_7_out, not_29_out, not_30_out);
  not not_30 (not_30_out, nand_21_out);
  not not_31 (not_31_out, nand_23_out);
  nor nor_8 (nor_8_out, not_31_out, not_32_out);
  not not_32 (not_32_out, nand_24_out);
  not not_33 (not_33_out, nor_1_out);
  not not_34 (not_34_out, nor_2_out);
  not not_35 (not_35_out, nor_3_out);
  not not_36 (not_36_out, nor_4_out);
  not not_37 (not_37_out, nor_5_out);
  not not_38 (not_38_out, nor_6_out);
  not not_39 (not_39_out, nor_7_out);
  not not_40 (not_40_out, nor_8_out);
  not not_41 (not_41_out, nand_1_out);
  not not_42 (not_42_out, not_33_out);
  not not_43 (not_43_out, 1'b0);
  not not_44 (not_44_out, nand_4_out);
  not not_45 (not_45_out, not_34_out);
  not not_46 (not_46_out, not_90_out);
  not not_47 (not_47_out, nand_7_out);
  not not_48 (not_48_out, not_35_out);
  not not_49 (not_49_out, not_92_out);
  not not_50 (not_50_out, nand_10_out);
  not not_51 (not_51_out, not_36_out);
  not not_52 (not_52_out, not_94_out);
  not not_53 (not_53_out, nand_13_out);
  not not_54 (not_54_out, not_37_out);
  not not_55 (not_55_out, not_96_out);
  not not_56 (not_56_out, nand_16_out);
  not not_57 (not_57_out, not_38_out);
  not not_58 (not_58_out, not_98_out);
  not not_59 (not_59_out, nand_19_out);
  not not_60 (not_60_out, not_39_out);
  not not_61 (not_61_out, not_100_out);
  not not_62 (not_62_out, nand_22_out);
  not not_63 (not_63_out, not_40_out);
  not not_64 (not_64_out, not_102_out);
  nand nand_25 (nand_25_out, not_33_out, not_43_out);
  nand nand_26 (nand_26_out, not_42_out, 1'b0);
  nand nand_27 (nand_27_out, not_33_out, 1'b0);
  nand nand_28 (nand_28_out, not_34_out, not_46_out);
  nand nand_29 (nand_29_out, not_45_out, not_90_out);
  nand nand_30 (nand_30_out, not_34_out, not_90_out);
  nand nand_31 (nand_31_out, not_35_out, not_49_out);
  nand nand_32 (nand_32_out, not_48_out, not_92_out);
  nand nand_33 (nand_33_out, not_35_out, not_92_out);
  nand nand_34 (nand_34_out, not_36_out, not_52_out);
  nand nand_35 (nand_35_out, not_51_out, not_94_out);
  nand nand_36 (nand_36_out, not_36_out, not_94_out);
  nand nand_37 (nand_37_out, not_37_out, not_55_out);
  nand nand_38 (nand_38_out, not_54_out, not_96_out);
  nand nand_39 (nand_39_out, not_37_out, not_96_out);
  nand nand_40 (nand_40_out, not_38_out, not_58_out);
  nand nand_41 (nand_41_out, not_57_out, not_98_out);
  nand nand_42 (nand_42_out, not_38_out, not_98_out);
  nand nand_43 (nand_43_out, not_39_out, not_61_out);
  nand nand_44 (nand_44_out, not_60_out, not_100_out);
  nand nand_45 (nand_45_out, not_39_out, not_100_out);
  nand nand_46 (nand_46_out, not_40_out, not_64_out);
  nand nand_47 (nand_47_out, not_63_out, not_102_out);
  nand nand_48 (nand_48_out, not_40_out, not_102_out);
  not not_65 (not_65_out, nand_25_out);
  nor nor_9 (nor_9_out, not_65_out, not_66_out);
  not not_66 (not_66_out, nand_26_out);
  nor nor_10 (nor_10_out, not_41_out, not_67_out);
  not not_67 (not_67_out, nand_27_out);
  not not_68 (not_68_out, nand_28_out);
  nor nor_11 (nor_11_out, not_68_out, not_69_out);
  not not_69 (not_69_out, nand_29_out);
  nor nor_12 (nor_12_out, not_44_out, not_70_out);
  not not_70 (not_70_out, nand_30_out);
  not not_71 (not_71_out, nand_31_out);
  nor nor_13 (nor_13_out, not_71_out, not_72_out);
  not not_72 (not_72_out, nand_32_out);
  nor nor_14 (nor_14_out, not_47_out, not_73_out);
  not not_73 (not_73_out, nand_33_out);
  not not_74 (not_74_out, nand_34_out);
  nor nor_15 (nor_15_out, not_74_out, not_75_out);
  not not_75 (not_75_out, nand_35_out);
  nor nor_16 (nor_16_out, not_50_out, not_76_out);
  not not_76 (not_76_out, nand_36_out);
  not not_77 (not_77_out, nand_37_out);
  nor nor_17 (nor_17_out, not_77_out, not_78_out);
  not not_78 (not_78_out, nand_38_out);
  nor nor_18 (nor_18_out, not_53_out, not_79_out);
  not not_79 (not_79_out, nand_39_out);
  not not_80 (not_80_out, nand_40_out);
  nor nor_19 (nor_19_out, not_80_out, not_81_out);
  not not_81 (not_81_out, nand_41_out);
  nor nor_20 (nor_20_out, not_56_out, not_82_out);
  not not_82 (not_82_out, nand_42_out);
  not not_83 (not_83_out, nand_43_out);
  nor nor_21 (nor_21_out, not_83_out, not_84_out);
  not not_84 (not_84_out, nand_44_out);
  nor nor_22 (nor_22_out, not_59_out, not_85_out);
  not not_85 (not_85_out, nand_45_out);
  not not_86 (not_86_out, nand_46_out);
  nor nor_23 (nor_23_out, not_86_out, not_87_out);
  not not_87 (not_87_out, nand_47_out);
  nor nor_24 (nor_24_out, not_62_out, not_88_out);
  not not_88 (not_88_out, nand_48_out);
  not not_89 (Sum0, nor_9_out);
  not not_90 (not_90_out, nor_10_out);
  not not_91 (Sum1, nor_11_out);
  not not_92 (not_92_out, nor_12_out);
  not not_93 (Sum2, nor_13_out);
  not not_94 (not_94_out, nor_14_out);
  not not_95 (Sum3, nor_15_out);
  not not_96 (not_96_out, nor_16_out);
  not not_97 (Sum4, nor_17_out);
  not not_98 (not_98_out, nor_18_out);
  not not_99 (Sum5, nor_19_out);
  not not_100 (not_100_out, nor_20_out);
  not not_101 (Sum6, nor_21_out);
  not not_102 (not_102_out, nor_22_out);
  not not_103 (Sum7, nor_23_out);
  not not_104 (C_out7, nor_24_out);
endmodule
