// Digital circuit MUX_2b.dig as structural Verilog
module MUX_2b (
  input  D0,
  input  S_select,
  input  D1,
  output out_4
);

  wire nand_1_out, nand_2_out, nand_3_out, nor_1_out, not_1_out, not_2_out, not_3_out, not_4_out;

  not not_1 (not_1_out, S_select);
  nand nand_1 (nand_1_out, D0, S_select);
  nand nand_2 (nand_2_out, not_1_out, D1);
  nand nand_3 (nand_3_out, D0, D1);
  not not_2 (not_2_out, nand_1_out);
  not not_3 (not_3_out, nand_2_out);
  not not_4 (not_4_out, nand_3_out);
  nor nor_1 (nor_1_out, not_2_out, not_3_out, not_4_out);
  not not_5 (out_4, nor_1_out);
endmodule
