// Digital circuit MUX_8b.dig as structural Verilog
module MUX_8b (
  input  D0_0,
  input  D1_0,
  input  D0_1,
  input  D1_1,
  input  D0_2,
  input  D1_2,
  input  D0_3,
  input  D1_3,
  input  D0_4,
  input  D1_4,
  input  D0_5,
  input  D1_5,
  input  D0_6,
  input  D1_6,
  input  D0_7,
  input  D1_7,
  input  S_select,
  output OUT0,
  output OUT1,
  output OUT2,
  output OUT3,
  output OUT4,
  output OUT5,
  output OUT6,
  output OUT7
);

  wire nand_1_out, nand_2_out, nand_3_out, nand_4_out, nand_5_out, nand_6_out, nand_7_out, nand_8_out,
       nand_9_out, nand_10_out, nand_11_out, nand_12_out, nand_13_out, nand_14_out, nand_15_out, nand_16_out,
       nand_17_out, nand_18_out, nand_19_out, nand_20_out, nand_21_out, nand_22_out, nand_23_out,
       nand_24_out, nor_1_out, nor_2_out, nor_3_out, nor_4_out, nor_5_out, nor_6_out, nor_7_out, nor_8_out,
       not_1_out, not_2_out, not_3_out, not_4_out, not_5_out, not_6_out, not_7_out, not_8_out, not_9_out,
       not_10_out, not_11_out, not_12_out, not_13_out, not_14_out, not_15_out, not_16_out, not_17_out,
       not_18_out, not_19_out, not_20_out, not_21_out, not_22_out, not_23_out, not_24_out, not_25_out;

  not not_1 (not_1_out, S_select);
  nand nand_1 (nand_1_out, D0_0, S_select);
  nand nand_2 (nand_2_out, not_1_out, D1_0);
  nand nand_3 (nand_3_out, D0_0, D1_0);
  nand nand_4 (nand_4_out, D0_1, S_select);
  nand nand_5 (nand_5_out, not_1_out, D1_1);
  nand nand_6 (nand_6_out, D0_1, D1_1);
  nand nand_7 (nand_7_out, D0_2, S_select);
  nand nand_8 (nand_8_out, not_1_out, D1_2);
  nand nand_9 (nand_9_out, D0_2, D1_2);
  nand nand_10 (nand_10_out, D0_3, S_select);
  nand nand_11 (nand_11_out, not_1_out, D1_3);
  nand nand_12 (nand_12_out, D0_3, D1_3);
  nand nand_13 (nand_13_out, D0_4, S_select);
  nand nand_14 (nand_14_out, not_1_out, D1_4);
  nand nand_15 (nand_15_out, D0_4, D1_4);
  nand nand_16 (nand_16_out, D0_5, S_select);
  nand nand_17 (nand_17_out, not_1_out, D1_5);
  nand nand_18 (nand_18_out, D0_5, D1_5);
  nand nand_19 (nand_19_out, D0_6, S_select);
  nand nand_20 (nand_20_out, not_1_out, D1_6);
  nand nand_21 (nand_21_out, D0_6, D1_6);
  nand nand_22 (nand_22_out, D0_7, S_select);
  nand nand_23 (nand_23_out, not_1_out, D1_7);
  nand nand_24 (nand_24_out, D0_7, D1_7);
  not not_2 (not_2_out, nand_1_out);
  not not_3 (not_3_out, nand_2_out);
  not not_4 (not_4_out, nand_3_out);
  not not_5 (not_5_out, nand_4_out);
  not not_6 (not_6_out, nand_5_out);
  not not_7 (not_7_out, nand_6_out);
  not not_8 (not_8_out, nand_7_out);
  not not_9 (not_9_out, nand_8_out);
  not not_10 (not_10_out, nand_9_out);
  not not_11 (not_11_out, nand_10_out);
  not not_12 (not_12_out, nand_11_out);
  not not_13 (not_13_out, nand_12_out);
  not not_14 (not_14_out, nand_13_out);
  not not_15 (not_15_out, nand_14_out);
  not not_16 (not_16_out, nand_15_out);
  not not_17 (not_17_out, nand_16_out);
  not not_18 (not_18_out, nand_17_out);
  not not_19 (not_19_out, nand_18_out);
  not not_20 (not_20_out, nand_19_out);
  not not_21 (not_21_out, nand_20_out);
  not not_22 (not_22_out, nand_21_out);
  not not_23 (not_23_out, nand_22_out);
  not not_24 (not_24_out, nand_23_out);
  not not_25 (not_25_out, nand_24_out);
  nor nor_1 (nor_1_out, not_2_out, not_3_out, not_4_out);
  nor nor_2 (nor_2_out, not_5_out, not_6_out, not_7_out);
  nor nor_3 (nor_3_out, not_8_out, not_9_out, not_10_out);
  nor nor_4 (nor_4_out, not_11_out, not_12_out, not_13_out);
  nor nor_5 (nor_5_out, not_14_out, not_15_out, not_16_out);
  nor nor_6 (nor_6_out, not_17_out, not_18_out, not_19_out);
  nor nor_7 (nor_7_out, not_20_out, not_21_out, not_22_out);
  nor nor_8 (nor_8_out, not_23_out, not_24_out, not_25_out);
  not not_26 (OUT0, nor_1_out);
  not not_27 (OUT1, nor_2_out);
  not not_28 (OUT2, nor_3_out);
  not not_29 (OUT3, nor_4_out);
  not not_30 (OUT4, nor_5_out);
  not not_31 (OUT5, nor_6_out);
  not not_32 (OUT6, nor_7_out);
  not not_33 (OUT7, nor_8_out);
endmodule
