// Digital circuit ROM_16_8b.dig as structural Verilog
module ROM_16_8b (
  input  INP3,
  input  INP2,
  input  INP1,
  input  INP0
);

  wire driver_1_out, driver_65_out, nand_1_out, nand_2_out, nand_3_out, nand_4_out, nand_5_out, nand_6_out,
       nand_7_out, nand_8_out, nand_9_out, nand_10_out, nand_11_out, nand_12_out, nand_13_out, nand_14_out,
       nand_15_out, nand_16_out, nand_17_out, not_1_out, not_2_out, not_3_out, not_4_out, not_5_out,
       not_6_out, not_7_out, not_8_out, not_9_out, not_10_out, not_11_out, not_12_out, not_13_out,
       not_14_out, not_15_out, not_16_out, not_17_out, not_18_out, not_19_out, not_20_out, not_21_out,
       not_22_out, not_23_out, not_24_out, not_25_out, not_26_out, not_27_out, not_28_out, not_29_out,
       not_30_out, not_31_out, not_32_out, not_33_out, not_34_out, not_35_out, not_36_out, not_37_out,
       not_38_out, not_39_out, not_40_out, not_41_out, not_42_out, not_43_out, not_44_out, not_45_out,
       not_46_out, not_47_out, not_48_out, not_49_out, not_50_out, not_51_out, not_52_out, not_53_out,
       not_54_out, not_55_out, not_56_out, not_57_out, not_58_out, not_59_out, not_60_out, not_61_out,
       not_62_out, not_63_out, not_64_out, not_65_out, not_66_out, not_67_out, not_68_out, not_69_out,
       not_70_out, not_71_out, not_72_out, not_73_out, not_74_out, not_75_out, not_76_out, not_77_out,
       not_78_out, not_79_out, not_80_out, not_81_out, not_82_out, not_83_out, not_84_out, not_85_out,
       not_86_out, not_87_out, not_88_out, not_89_out, not_90_out, not_91_out, not_92_out, not_93_out,
       not_94_out, not_95_out, not_96_out, not_97_out, not_98_out, not_99_out, not_100_out, not_101_out,
       not_102_out, not_103_out, not_104_out, not_105_out, not_106_out, not_107_out, not_108_out,
       not_109_out, not_110_out, not_111_out, not_112_out, not_113_out, not_114_out, not_115_out,
       not_116_out, not_117_out, not_118_out, not_119_out, not_120_out, not_121_out, not_122_out,
       not_123_out, not_124_out, not_125_out, not_126_out, not_127_out, not_128_out, not_129_out,
       not_130_out, not_131_out, not_132_out, not_133_out, not_134_out, not_135_out, not_136_out,
       not_137_out, not_138_out, not_139_out, not_140_out, not_141_out, not_142_out, not_143_out,
       not_144_out, not_145_out, not_146_out, not_147_out, not_148_out, not_149_out;

  not not_1 (not_1_out, 1'b1);
  assign driver_1_out = not_25_out ? not_1_out : 1'bz;  // Driver driver_1
  not not_2 (not_2_out, 1'b1);
  assign driver_1_out = not_25_out ? not_2_out : 1'bz;  // Driver driver_2
  not not_3 (not_3_out, 1'b1);
  assign driver_1_out = not_25_out ? not_3_out : 1'bz;  // Driver driver_3
  not not_4 (not_4_out, 1'b1);
  assign driver_1_out = not_25_out ? not_4_out : 1'bz;  // Driver driver_4
  not not_5 (not_5_out, 1'b1);
  assign driver_1_out = not_25_out ? not_5_out : 1'bz;  // Driver driver_5
  not not_6 (not_6_out, 1'b1);
  assign driver_1_out = not_25_out ? not_6_out : 1'bz;  // Driver driver_6
  not not_7 (not_7_out, 1'b1);
  assign driver_1_out = not_25_out ? not_7_out : 1'bz;  // Driver driver_7
  not not_8 (not_8_out, 1'b1);
  assign driver_1_out = not_25_out ? not_8_out : 1'bz;  // Driver driver_8
  not not_9 (not_9_out, 1'b1);
  assign driver_1_out = not_35_out ? not_9_out : 1'bz;  // Driver driver_9
  not not_10 (not_10_out, 1'b1);
  assign driver_1_out = not_35_out ? not_10_out : 1'bz;  // Driver driver_10
  not not_11 (not_11_out, 1'b1);
  assign driver_1_out = not_35_out ? not_11_out : 1'bz;  // Driver driver_11
  not not_12 (not_12_out, 1'b1);
  assign driver_1_out = not_35_out ? not_12_out : 1'bz;  // Driver driver_12
  not not_13 (not_13_out, 1'b1);
  assign driver_1_out = not_35_out ? not_13_out : 1'bz;  // Driver driver_13
  not not_14 (not_14_out, 1'b1);
  assign driver_1_out = not_35_out ? not_14_out : 1'bz;  // Driver driver_14
  not not_15 (not_15_out, 1'b1);
  assign driver_1_out = not_35_out ? not_15_out : 1'bz;  // Driver driver_15
  not not_16 (not_16_out, 1'b1);
  assign driver_1_out = not_35_out ? not_16_out : 1'bz;  // Driver driver_16
  not not_17 (not_17_out, 1'b1);
  assign driver_1_out = not_36_out ? not_17_out : 1'bz;  // Driver driver_17
  not not_18 (not_18_out, 1'b1);
  assign driver_1_out = not_36_out ? not_18_out : 1'bz;  // Driver driver_18
  not not_19 (not_19_out, 1'b1);
  assign driver_1_out = not_36_out ? not_19_out : 1'bz;  // Driver driver_19
  not not_20 (not_20_out, 1'b1);
  assign driver_1_out = not_36_out ? not_20_out : 1'bz;  // Driver driver_20
  not not_21 (not_21_out, 1'b1);
  assign driver_1_out = not_36_out ? not_21_out : 1'bz;  // Driver driver_21
  not not_22 (not_22_out, 1'b1);
  assign driver_1_out = not_36_out ? not_22_out : 1'bz;  // Driver driver_22
  not not_23 (not_23_out, 1'b1);
  assign driver_1_out = not_36_out ? not_23_out : 1'bz;  // Driver driver_23
  not not_24 (not_24_out, 1'b1);
  assign driver_1_out = not_36_out ? not_24_out : 1'bz;  // Driver driver_24
  nand nand_1 (nand_1_out, INP0, INP1, INP2, INP3);
  not not_25 (not_25_out, nand_1_out);
  not not_26 (not_26_out, 1'b1);
  assign driver_1_out = not_45_out ? not_26_out : 1'bz;  // Driver driver_25
  not not_27 (not_27_out, 1'b1);
  assign driver_1_out = not_45_out ? not_27_out : 1'bz;  // Driver driver_26
  not not_28 (not_28_out, 1'b1);
  assign driver_1_out = not_45_out ? not_28_out : 1'bz;  // Driver driver_27
  not not_29 (not_29_out, 1'b1);
  assign driver_1_out = not_45_out ? not_29_out : 1'bz;  // Driver driver_28
  not not_30 (not_30_out, 1'b1);
  assign driver_1_out = not_45_out ? not_30_out : 1'bz;  // Driver driver_29
  not not_31 (not_31_out, 1'b1);
  assign driver_1_out = not_45_out ? not_31_out : 1'bz;  // Driver driver_30
  not not_32 (not_32_out, 1'b1);
  assign driver_1_out = not_45_out ? not_32_out : 1'bz;  // Driver driver_31
  not not_33 (not_33_out, 1'b1);
  assign driver_1_out = not_45_out ? not_33_out : 1'bz;  // Driver driver_32
  not not_34 (not_34_out, INP3);
  not not_35 (not_35_out, nand_2_out);
  nand nand_2 (nand_2_out, not_107_out, INP1, INP2, INP3);
  nand nand_3 (nand_3_out, INP0, not_86_out, INP2, INP3);
  not not_36 (not_36_out, nand_3_out);
  not not_37 (not_37_out, 1'b1);
  assign driver_1_out = not_46_out ? not_37_out : 1'bz;  // Driver driver_33
  not not_38 (not_38_out, 1'b1);
  assign driver_1_out = not_46_out ? not_38_out : 1'bz;  // Driver driver_34
  not not_39 (not_39_out, 1'b1);
  assign driver_1_out = not_46_out ? not_39_out : 1'bz;  // Driver driver_35
  not not_40 (not_40_out, 1'b1);
  assign driver_1_out = not_46_out ? not_40_out : 1'bz;  // Driver driver_36
  not not_41 (not_41_out, 1'b1);
  assign driver_1_out = not_46_out ? not_41_out : 1'bz;  // Driver driver_37
  not not_42 (not_42_out, 1'b1);
  assign driver_1_out = not_46_out ? not_42_out : 1'bz;  // Driver driver_38
  not not_43 (not_43_out, 1'b1);
  assign driver_1_out = not_46_out ? not_43_out : 1'bz;  // Driver driver_39
  not not_44 (not_44_out, 1'b1);
  assign driver_1_out = not_46_out ? not_44_out : 1'bz;  // Driver driver_40
  not not_45 (not_45_out, nand_4_out);
  nand nand_4 (nand_4_out, not_107_out, not_86_out, INP2, INP3);
  nand nand_5 (nand_5_out, INP0, INP1, not_56_out, INP3);
  not not_46 (not_46_out, nand_5_out);
  not not_47 (not_47_out, 1'b1);
  assign driver_1_out = not_55_out ? not_47_out : 1'bz;  // Driver driver_41
  not not_48 (not_48_out, 1'b1);
  assign driver_1_out = not_55_out ? not_48_out : 1'bz;  // Driver driver_42
  not not_49 (not_49_out, 1'b1);
  assign driver_1_out = not_55_out ? not_49_out : 1'bz;  // Driver driver_43
  not not_50 (not_50_out, 1'b1);
  assign driver_1_out = not_55_out ? not_50_out : 1'bz;  // Driver driver_44
  not not_51 (not_51_out, 1'b1);
  assign driver_1_out = not_55_out ? not_51_out : 1'bz;  // Driver driver_45
  not not_52 (not_52_out, 1'b1);
  assign driver_1_out = not_55_out ? not_52_out : 1'bz;  // Driver driver_46
  not not_53 (not_53_out, 1'b1);
  assign driver_1_out = not_55_out ? not_53_out : 1'bz;  // Driver driver_47
  not not_54 (not_54_out, 1'b1);
  assign driver_1_out = not_55_out ? not_54_out : 1'bz;  // Driver driver_48
  not not_55 (not_55_out, nand_6_out);
  not not_56 (not_56_out, INP2);
  nand nand_6 (nand_6_out, not_107_out, INP1, not_56_out, INP3);
  nand nand_7 (nand_7_out, INP0, not_86_out, not_56_out, INP3);
  not not_57 (not_57_out, nand_7_out);
  not not_58 (not_58_out, 1'b1);
  assign driver_1_out = not_57_out ? not_58_out : 1'bz;  // Driver driver_49
  not not_59 (not_59_out, 1'b1);
  assign driver_1_out = not_57_out ? not_59_out : 1'bz;  // Driver driver_50
  not not_60 (not_60_out, 1'b1);
  assign driver_1_out = not_57_out ? not_60_out : 1'bz;  // Driver driver_51
  not not_61 (not_61_out, 1'b1);
  assign driver_1_out = not_57_out ? not_61_out : 1'bz;  // Driver driver_52
  not not_62 (not_62_out, 1'b1);
  assign driver_1_out = not_57_out ? not_62_out : 1'bz;  // Driver driver_53
  not not_63 (not_63_out, 1'b1);
  assign driver_1_out = not_57_out ? not_63_out : 1'bz;  // Driver driver_54
  not not_64 (not_64_out, 1'b1);
  assign driver_1_out = not_57_out ? not_64_out : 1'bz;  // Driver driver_55
  not not_65 (not_65_out, 1'b1);
  assign driver_1_out = not_57_out ? not_65_out : 1'bz;  // Driver driver_56
  not not_66 (not_66_out, nand_8_out);
  nand nand_8 (nand_8_out, not_107_out, not_86_out, not_56_out, INP3);
  not not_67 (not_67_out, nand_9_out);
  not not_68 (not_68_out, 1'b1);
  assign driver_1_out = not_66_out ? not_68_out : 1'bz;  // Driver driver_57
  not not_69 (not_69_out, 1'b1);
  assign driver_1_out = not_66_out ? not_69_out : 1'bz;  // Driver driver_58
  not not_70 (not_70_out, 1'b1);
  assign driver_1_out = not_66_out ? not_70_out : 1'bz;  // Driver driver_59
  not not_71 (not_71_out, 1'b1);
  assign driver_1_out = not_66_out ? not_71_out : 1'bz;  // Driver driver_60
  not not_72 (not_72_out, 1'b1);
  assign driver_1_out = not_66_out ? not_72_out : 1'bz;  // Driver driver_61
  not not_73 (not_73_out, 1'b1);
  assign driver_1_out = not_66_out ? not_73_out : 1'bz;  // Driver driver_62
  not not_74 (not_74_out, 1'b1);
  assign driver_1_out = not_66_out ? not_74_out : 1'bz;  // Driver driver_63
  not not_75 (not_75_out, 1'b1);
  assign driver_1_out = not_66_out ? not_75_out : 1'bz;  // Driver driver_64
  nand nand_9 (nand_9_out, INP0, INP1, INP2, not_34_out);
  nand nand_10 (nand_10_out, not_107_out, INP1, INP2, not_34_out);
  not not_76 (not_76_out, nand_10_out);
  not not_77 (not_77_out, nand_11_out);
  not not_78 (not_78_out, 1'b0);
  assign driver_65_out = not_67_out ? not_78_out : 1'bz;  // Driver driver_65
  not not_79 (not_79_out, 1'b0);
  assign driver_65_out = not_67_out ? not_79_out : 1'bz;  // Driver driver_66
  not not_80 (not_80_out, 1'b1);
  assign driver_1_out = not_67_out ? not_80_out : 1'bz;  // Driver driver_67
  not not_81 (not_81_out, 1'b0);
  assign driver_65_out = not_67_out ? not_81_out : 1'bz;  // Driver driver_68
  not not_82 (not_82_out, 1'b1);
  assign driver_1_out = not_67_out ? not_82_out : 1'bz;  // Driver driver_69
  not not_83 (not_83_out, 1'b1);
  assign driver_1_out = not_67_out ? not_83_out : 1'bz;  // Driver driver_70
  not not_84 (not_84_out, 1'b1);
  assign driver_1_out = not_67_out ? not_84_out : 1'bz;  // Driver driver_71
  not not_85 (not_85_out, 1'b1);
  assign driver_1_out = not_67_out ? not_85_out : 1'bz;  // Driver driver_72
  not not_86 (not_86_out, INP1);
  nand nand_11 (nand_11_out, INP0, not_86_out, INP2, not_34_out);
  nand nand_12 (nand_12_out, not_107_out, not_86_out, INP2, not_34_out);
  not not_87 (not_87_out, nand_12_out);
  not not_88 (not_88_out, nand_13_out);
  not not_89 (not_89_out, 1'b1);
  assign driver_1_out = not_76_out ? not_89_out : 1'bz;  // Driver driver_73
  not not_90 (not_90_out, 1'b1);
  assign driver_1_out = not_76_out ? not_90_out : 1'bz;  // Driver driver_74
  not not_91 (not_91_out, 1'b1);
  assign driver_1_out = not_76_out ? not_91_out : 1'bz;  // Driver driver_75
  not not_92 (not_92_out, 1'b1);
  assign driver_1_out = not_76_out ? not_92_out : 1'bz;  // Driver driver_76
  not not_93 (not_93_out, 1'b1);
  assign driver_1_out = not_76_out ? not_93_out : 1'bz;  // Driver driver_77
  not not_94 (not_94_out, 1'b0);
  assign driver_65_out = not_76_out ? not_94_out : 1'bz;  // Driver driver_78
  not not_95 (not_95_out, 1'b1);
  assign driver_1_out = not_76_out ? not_95_out : 1'bz;  // Driver driver_79
  not not_96 (not_96_out, 1'b0);
  assign driver_65_out = not_76_out ? not_96_out : 1'bz;  // Driver driver_80
  nand nand_13 (nand_13_out, INP0, INP1, not_56_out, not_34_out);
  nand nand_14 (nand_14_out, not_107_out, INP1, not_56_out, not_34_out);
  not not_97 (not_97_out, nand_14_out);
  not not_98 (not_98_out, nand_15_out);
  not not_99 (not_99_out, 1'b0);
  assign driver_65_out = not_77_out ? not_99_out : 1'bz;  // Driver driver_81
  not not_100 (not_100_out, 1'b0);
  assign driver_65_out = not_77_out ? not_100_out : 1'bz;  // Driver driver_82
  not not_101 (not_101_out, 1'b0);
  assign driver_65_out = not_77_out ? not_101_out : 1'bz;  // Driver driver_83
  not not_102 (not_102_out, 1'b1);
  assign driver_1_out = not_77_out ? not_102_out : 1'bz;  // Driver driver_84
  not not_103 (not_103_out, 1'b1);
  assign driver_1_out = not_77_out ? not_103_out : 1'bz;  // Driver driver_85
  not not_104 (not_104_out, 1'b1);
  assign driver_1_out = not_77_out ? not_104_out : 1'bz;  // Driver driver_86
  not not_105 (not_105_out, 1'b1);
  assign driver_1_out = not_77_out ? not_105_out : 1'bz;  // Driver driver_87
  not not_106 (not_106_out, 1'b1);
  assign driver_1_out = not_77_out ? not_106_out : 1'bz;  // Driver driver_88
  nand nand_15 (nand_15_out, INP0, not_86_out, not_56_out, not_34_out);
  not not_107 (not_107_out, INP0);
  nand nand_16 (nand_16_out, not_107_out, not_86_out, not_56_out, not_34_out);
  not not_108 (not_108_out, nand_16_out);
  not not_109 (not_109_out, 1'b1);
  assign driver_1_out = not_87_out ? not_109_out : 1'bz;  // Driver driver_89
  not not_110 (not_110_out, 1'b1);
  assign driver_1_out = not_87_out ? not_110_out : 1'bz;  // Driver driver_90
  not not_111 (not_111_out, 1'b1);
  assign driver_1_out = not_87_out ? not_111_out : 1'bz;  // Driver driver_91
  not not_112 (not_112_out, 1'b1);
  assign driver_1_out = not_87_out ? not_112_out : 1'bz;  // Driver driver_92
  not not_113 (not_113_out, 1'b1);
  assign driver_1_out = not_87_out ? not_113_out : 1'bz;  // Driver driver_93
  not not_114 (not_114_out, 1'b1);
  assign driver_1_out = not_87_out ? not_114_out : 1'bz;  // Driver driver_94
  not not_115 (not_115_out, 1'b0);
  assign driver_65_out = not_87_out ? not_115_out : 1'bz;  // Driver driver_95
  not not_116 (not_116_out, 1'b0);
  assign driver_65_out = not_87_out ? not_116_out : 1'bz;  // Driver driver_96
  not not_117 (not_117_out, 1'b1);
  assign driver_1_out = not_88_out ? not_117_out : 1'bz;  // Driver driver_97
  not not_118 (not_118_out, 1'b1);
  assign driver_1_out = not_88_out ? not_118_out : 1'bz;  // Driver driver_98
  not not_119 (not_119_out, 1'b1);
  assign driver_1_out = not_88_out ? not_119_out : 1'bz;  // Driver driver_99
  not not_120 (not_120_out, 1'b1);
  assign driver_1_out = not_88_out ? not_120_out : 1'bz;  // Driver driver_100
  not not_121 (not_121_out, 1'b1);
  assign driver_1_out = not_88_out ? not_121_out : 1'bz;  // Driver driver_101
  not not_122 (not_122_out, 1'b0);
  assign driver_65_out = not_88_out ? not_122_out : 1'bz;  // Driver driver_102
  not not_123 (not_123_out, 1'b0);
  assign driver_65_out = not_88_out ? not_123_out : 1'bz;  // Driver driver_103
  not not_124 (not_124_out, 1'b0);
  assign driver_65_out = not_88_out ? not_124_out : 1'bz;  // Driver driver_104
  not not_125 (not_125_out, 1'b1);
  assign driver_1_out = not_97_out ? not_125_out : 1'bz;  // Driver driver_105
  not not_126 (not_126_out, 1'b1);
  assign driver_1_out = not_97_out ? not_126_out : 1'bz;  // Driver driver_106
  not not_127 (not_127_out, 1'b1);
  assign driver_1_out = not_97_out ? not_127_out : 1'bz;  // Driver driver_107
  not not_128 (not_128_out, 1'b1);
  assign driver_1_out = not_97_out ? not_128_out : 1'bz;  // Driver driver_108
  not not_129 (not_129_out, 1'b0);
  assign driver_65_out = not_97_out ? not_129_out : 1'bz;  // Driver driver_109
  not not_130 (not_130_out, 1'b0);
  assign driver_65_out = not_97_out ? not_130_out : 1'bz;  // Driver driver_110
  not not_131 (not_131_out, 1'b1);
  assign driver_1_out = not_97_out ? not_131_out : 1'bz;  // Driver driver_111
  not not_132 (not_132_out, 1'b1);
  assign driver_1_out = not_97_out ? not_132_out : 1'bz;  // Driver driver_112
  not not_133 (not_133_out, 1'b1);
  assign driver_1_out = not_98_out ? not_133_out : 1'bz;  // Driver driver_113
  not not_134 (not_134_out, 1'b1);
  assign driver_1_out = not_98_out ? not_134_out : 1'bz;  // Driver driver_114
  not not_135 (not_135_out, 1'b1);
  assign driver_1_out = not_98_out ? not_135_out : 1'bz;  // Driver driver_115
  not not_136 (not_136_out, 1'b1);
  assign driver_1_out = not_98_out ? not_136_out : 1'bz;  // Driver driver_116
  not not_137 (not_137_out, 1'b0);
  assign driver_65_out = not_98_out ? not_137_out : 1'bz;  // Driver driver_117
  not not_138 (not_138_out, 1'b0);
  assign driver_65_out = not_98_out ? not_138_out : 1'bz;  // Driver driver_118
  not not_139 (not_139_out, 1'b0);
  assign driver_65_out = not_98_out ? not_139_out : 1'bz;  // Driver driver_119
  not not_140 (not_140_out, 1'b0);
  assign driver_65_out = not_98_out ? not_140_out : 1'bz;  // Driver driver_120
  not not_141 (not_141_out, 1'b1);
  assign driver_1_out = not_108_out ? not_141_out : 1'bz;  // Driver driver_121
  not not_142 (not_142_out, 1'b1);
  assign driver_1_out = not_108_out ? not_142_out : 1'bz;  // Driver driver_122
  not not_143 (not_143_out, 1'b1);
  assign driver_1_out = not_108_out ? not_143_out : 1'bz;  // Driver driver_123
  not not_144 (not_144_out, 1'b1);
  assign driver_1_out = not_108_out ? not_144_out : 1'bz;  // Driver driver_124
  not not_145 (not_145_out, 1'b1);
  assign driver_1_out = not_108_out ? not_145_out : 1'bz;  // Driver driver_125
  not not_146 (not_146_out, 1'b1);
  assign driver_1_out = not_108_out ? not_146_out : 1'bz;  // Driver driver_126
  not not_147 (not_147_out, 1'b1);
  assign driver_1_out = not_108_out ? not_147_out : 1'bz;  // Driver driver_127
  not not_148 (not_148_out, 1'b1);
  assign driver_1_out = not_108_out ? not_148_out : 1'bz;  // Driver driver_128
  nand nand_17 (nand_17_out, driver_65_out, driver_1_out);
  not not_149 (not_149_out, nand_17_out);
  LED led_1 (.in(not_149_out));

  // Notes on the sheet:
  //   1
  //   0
  //   0-phase
  //   1-phase
endmodule
