// Digital circuit SRAM_2b.dig as structural Verilog
module SRAM_2b (
  input  Data,
  input  CLK,
  input  CLK_2,
  input  Data_2,
  input  Data_3,
  input  CLK_3,
  input  CLK_4,
  input  Data_4,
  output Q,
  output Q_2,
  output Q_3,
  output Q_4,
  output Q_5,
  output Q_6,
  output Q_7,
  output Q_8,
  output Q_9,
  output Q_10,
  output Q_11,
  output Q_12,
  output Q_13,
  output Q_14,
  output Q_15,
  output Q_16
);

  wire nand_1_out, nand_2_out, nand_3_out, nand_4_out, nand_9_out, nand_10_out, nand_11_out, nand_12_out,
       nand_17_out, nand_18_out, nand_19_out, nand_20_out, nand_25_out, nand_26_out, nand_27_out,
       nand_28_out, not_1_out, not_2_out, not_3_out, not_4_out, not_5_out, not_6_out, not_7_out, not_8_out;

  not not_1 (not_1_out, Data_3);
  not not_2 (not_2_out, Q_9);
  nand nand_1 (nand_1_out, Data_3, CLK_3);
  nand nand_2 (nand_2_out, not_1_out, CLK_3);
  nand nand_3 (nand_3_out, Q_9, CLK_4);
  nand nand_4 (nand_4_out, not_2_out, CLK_4);
  nand nand_5 (Q_9, nand_1_out, Q_10);
  nand nand_6 (Q_10, Q_9, nand_2_out);
  nand nand_7 (Q_11, nand_3_out, Q_12);
  nand nand_8 (Q_12, Q_11, nand_4_out);
  not not_3 (not_3_out, Data_4);
  not not_4 (not_4_out, Q_13);
  nand nand_9 (nand_9_out, Data_4, CLK_3);
  nand nand_10 (nand_10_out, not_3_out, CLK_3);
  nand nand_11 (nand_11_out, Q_13, CLK_4);
  nand nand_12 (nand_12_out, not_4_out, CLK_4);
  nand nand_13 (Q_13, nand_9_out, Q_14);
  nand nand_14 (Q_14, Q_13, nand_10_out);
  nand nand_15 (Q_15, nand_11_out, Q_16);
  nand nand_16 (Q_16, Q_15, nand_12_out);
  not not_5 (not_5_out, Data);
  not not_6 (not_6_out, Q);
  nand nand_17 (nand_17_out, CLK, Data);
  nand nand_18 (nand_18_out, CLK, not_5_out);
  nand nand_19 (nand_19_out, CLK_2, Q);
  nand nand_20 (nand_20_out, CLK_2, not_6_out);
  nand nand_21 (Q, nand_17_out, Q_2);
  nand nand_22 (Q_2, Q, nand_18_out);
  nand nand_23 (Q_3, nand_19_out, Q_4);
  nand nand_24 (Q_4, Q_3, nand_20_out);
  not not_7 (not_7_out, Data_2);
  not not_8 (not_8_out, Q_5);
  nand nand_25 (nand_25_out, CLK, Data_2);
  nand nand_26 (nand_26_out, CLK, not_7_out);
  nand nand_27 (nand_27_out, CLK_2, Q_5);
  nand nand_28 (nand_28_out, CLK_2, not_8_out);
  nand nand_29 (Q_5, nand_25_out, Q_6);
  nand nand_30 (Q_6, Q_5, nand_26_out);
  nand nand_31 (Q_7, nand_27_out, Q_8);
  nand nand_32 (Q_8, Q_7, nand_28_out);
endmodule
