// Digital circuit SRAM_8b LED.dig as structural Verilog
module SRAM_8b_LED (
  input  d0,
  input  \с0 ,
  input  \с1 ,
  input  d1,
  input  c2,
  input  c3,
  input  d2,
  input  d3,
  input  d4,
  input  d5,
  input  d6,
  input  d7,
  input  c4,
  input  c5,
  input  c6,
  input  c7,
  input  Data0,
  input  CLK0,
  input  CLK1,
  input  Data1,
  input  CLK2,
  input  CLK3,
  input  Data2,
  input  Data3,
  input  Data4,
  input  Data5,
  input  Data6,
  input  Data7,
  input  CLK4,
  input  CLK5,
  input  CLK6,
  input  CLK7,
  output out_17,
  output Q00,
  output Q1,
  output Q10,
  output Q9,
  output Q01,
  output Q2,
  output Q11,
  output Q10_2,
  output Q20,
  output Q17,
  output Q30,
  output Q25,
  output Q21,
  output Q18,
  output Q31,
  output Q26,
  output Q02,
  output Q3,
  output Q12,
  output Q11_2,
  output Q03,
  output Q4,
  output Q13,
  output Q12_2,
  output Q22,
  output Q19,
  output Q32,
  output Q27,
  output Q23,
  output Q20_2,
  output Q33,
  output Q28,
  output Q04,
  output Q5,
  output Q14,
  output Q13_2,
  output Q05,
  output Q6,
  output Q15,
  output Q14_2,
  output Q24,
  output Q21_2,
  output Q34,
  output Q29,
  output Q25_2,
  output Q22_2,
  output Q35,
  output Q30_2,
  output Q06,
  output Q7,
  output Q16,
  output Q15_2,
  output Q07,
  output Q8,
  output Q17_2,
  output Q16_2,
  output Q26_2,
  output Q23_2,
  output Q36,
  output Q31_2,
  output Q27_2,
  output Q24_2,
  output Q37,
  output Q32_2,
  output Q40,
  output Q33_2,
  output Q50,
  output Q41,
  output Q41_2,
  output Q34_2,
  output Q51,
  output Q42,
  output Q60,
  output Q49,
  output Q70,
  output Q57,
  output Q61,
  output Q50_2,
  output Q71,
  output Q58,
  output Q42_2,
  output Q35_2,
  output Q52,
  output Q43,
  output Q43_2,
  output Q36_2,
  output Q53,
  output Q44,
  output Q62,
  output Q51_2,
  output Q72,
  output Q59,
  output Q63,
  output Q52_2,
  output Q73,
  output Q60_2,
  output Q44_2,
  output Q37_2,
  output Q54,
  output Q45,
  output Q45_2,
  output Q38,
  output Q55,
  output Q46,
  output Q64,
  output Q53_2,
  output Q74,
  output Q61_2,
  output Q65,
  output Q54_2,
  output Q75,
  output Q62_2,
  output Q46_2,
  output Q39,
  output Q56,
  output Q47,
  output Q47_2,
  output Q40_2,
  output Q57_2,
  output Q48,
  output Q66,
  output Q55_2,
  output Q76,
  output Q63_2,
  output Q67,
  output Q56_2,
  output Q77,
  output Q64_2
);

  wire nand_1_out, nand_2_out, nand_3_out, nand_4_out, nand_6_out, nand_7_out, nand_8_out, nand_9_out,
       nand_10_out, nand_11_out, nand_12_out, nand_13_out, nand_14_out, nand_15_out, nand_16_out,
       nand_17_out, nand_18_out, nand_19_out, nand_20_out, nand_21_out, nand_22_out, nand_23_out,
       nand_24_out, nand_25_out, nand_26_out, nand_27_out, nand_28_out, nand_29_out, nand_30_out,
       nand_31_out, nand_32_out, nand_33_out, nand_50_out, nand_51_out, nand_52_out, nand_53_out,
       nand_54_out, nand_55_out, nand_56_out, nand_57_out, nand_58_out, nand_59_out, nand_60_out,
       nand_61_out, nand_62_out, nand_63_out, nand_64_out, nand_65_out, nand_82_out, nand_83_out,
       nand_84_out, nand_85_out, nand_86_out, nand_87_out, nand_88_out, nand_89_out, nand_90_out,
       nand_91_out, nand_92_out, nand_93_out, nand_94_out, nand_95_out, nand_96_out, nand_97_out,
       nand_114_out, nand_115_out, nand_116_out, nand_117_out, nand_118_out, nand_119_out, nand_120_out,
       nand_121_out, nand_122_out, nand_123_out, nand_124_out, nand_125_out, nand_126_out, nand_127_out,
       nand_128_out, nand_129_out, nand_146_out, nand_147_out, nand_148_out, nand_149_out, nand_150_out,
       nand_151_out, nand_152_out, nand_153_out, nand_154_out, nand_155_out, nand_156_out, nand_157_out,
       nand_158_out, nand_159_out, nand_160_out, nand_161_out, nand_178_out, nand_179_out, nand_180_out,
       nand_181_out, nand_182_out, nand_183_out, nand_184_out, nand_185_out, nand_186_out, nand_187_out,
       nand_188_out, nand_189_out, nand_190_out, nand_191_out, nand_192_out, nand_193_out, nand_210_out,
       nand_211_out, nand_212_out, nand_213_out, nand_214_out, nand_215_out, nand_216_out, nand_217_out,
       nand_218_out, nand_219_out, nand_220_out, nand_221_out, nand_222_out, nand_223_out, nand_224_out,
       nand_225_out, nand_242_out, nand_243_out, nand_244_out, nand_245_out, nand_246_out, nand_247_out,
       nand_248_out, nand_249_out, nand_250_out, nand_251_out, nand_252_out, nand_253_out, nand_254_out,
       nand_255_out, nand_256_out, nand_257_out, not_1_out, not_2_out, not_3_out, not_4_out, not_5_out,
       not_6_out, not_7_out, not_8_out, not_9_out, not_10_out, not_11_out, not_12_out, not_13_out,
       not_14_out, not_15_out, not_16_out, not_17_out, not_18_out, not_19_out, not_20_out, not_21_out,
       not_22_out, not_23_out, not_24_out, not_25_out, not_26_out, not_27_out, not_28_out, not_29_out,
       not_30_out, not_31_out, not_32_out, not_33_out, not_34_out, not_35_out, not_36_out, not_37_out,
       not_38_out, not_39_out, not_40_out, not_41_out, not_42_out, not_43_out, not_44_out, not_45_out,
       not_46_out, not_47_out, not_48_out, not_49_out, not_50_out, not_51_out, not_52_out, not_53_out,
       not_54_out, not_55_out, not_56_out, not_57_out, not_58_out, not_59_out, not_60_out, not_61_out,
       not_62_out, not_63_out, not_64_out, sram_8b_1_q00, sram_8b_1_q01, sram_8b_1_q1, sram_8b_1_q02,
       sram_8b_1_q2, sram_8b_1_q03, sram_8b_1_q3, sram_8b_1_q04, sram_8b_1_q4, sram_8b_1_q05, sram_8b_1_q5,
       sram_8b_1_q06, sram_8b_1_q6, sram_8b_1_q07, sram_8b_1_q7, sram_8b_1_q8, sram_8b_1_q9, sram_8b_1_q10,
       sram_8b_1_q10_2, sram_8b_1_q11, sram_8b_1_q11_2, sram_8b_1_q12, sram_8b_1_q12_2, sram_8b_1_q13,
       sram_8b_1_q13_2, sram_8b_1_q14, sram_8b_1_q14_2, sram_8b_1_q15, sram_8b_1_q15_2, sram_8b_1_q16,
       sram_8b_1_q16_2, sram_8b_1_q17, sram_8b_1_q17_2, sram_8b_1_q18, sram_8b_1_q19, sram_8b_1_q20,
       sram_8b_1_q20_2, sram_8b_1_q21, sram_8b_1_q21_2, sram_8b_1_q22, sram_8b_1_q22_2, sram_8b_1_q23,
       sram_8b_1_q23_2, sram_8b_1_q24, sram_8b_1_q24_2, sram_8b_1_q25, sram_8b_1_q25_2, sram_8b_1_q26,
       sram_8b_1_q26_2, sram_8b_1_q27, sram_8b_1_q27_2, sram_8b_1_q28, sram_8b_1_q29, sram_8b_1_q30,
       sram_8b_1_q30_2, sram_8b_1_q31, sram_8b_1_q31_2, sram_8b_1_q32, sram_8b_1_q32_2, sram_8b_1_q33,
       sram_8b_1_q33_2, sram_8b_1_q34, sram_8b_1_q34_2, sram_8b_1_q35, sram_8b_1_q35_2, sram_8b_1_q36,
       sram_8b_1_q36_2, sram_8b_1_q37, sram_8b_1_q37_2, sram_8b_1_q38, sram_8b_1_q39, sram_8b_1_q40,
       sram_8b_1_q40_2, sram_8b_1_q41, sram_8b_1_q41_2, sram_8b_1_q42, sram_8b_1_q42_2, sram_8b_1_q43,
       sram_8b_1_q43_2, sram_8b_1_q44, sram_8b_1_q44_2, sram_8b_1_q45, sram_8b_1_q45_2, sram_8b_1_q46,
       sram_8b_1_q46_2, sram_8b_1_q47, sram_8b_1_q47_2, sram_8b_1_q48, sram_8b_1_q49, sram_8b_1_q50,
       sram_8b_1_q50_2, sram_8b_1_q51, sram_8b_1_q51_2, sram_8b_1_q52, sram_8b_1_q52_2, sram_8b_1_q53,
       sram_8b_1_q53_2, sram_8b_1_q54, sram_8b_1_q54_2, sram_8b_1_q55, sram_8b_1_q55_2, sram_8b_1_q56,
       sram_8b_1_q56_2, sram_8b_1_q57, sram_8b_1_q57_2, sram_8b_1_q58, sram_8b_1_q59, sram_8b_1_q60,
       sram_8b_1_q60_2, sram_8b_1_q61, sram_8b_1_q61_2, sram_8b_1_q62, sram_8b_1_q62_2, sram_8b_1_q63,
       sram_8b_1_q63_2, sram_8b_1_q64, sram_8b_1_q65, sram_8b_1_q66, sram_8b_1_q67, sram_8b_1_q70,
       sram_8b_1_q71, sram_8b_1_q72, sram_8b_1_q73, sram_8b_1_q74, sram_8b_1_q75, sram_8b_1_q76,
       sram_8b_1_q77;

  SRAM_8b sram_8b_1 (
    .Data0(d0), .CLK0(\с0 ), .CLK1(\с1 ), .Data1(d1), .CLK2(c2), .CLK3(c3), .Data2(d2), .Data3(d3),
    .Data4(d4), .Data5(d5), .Data6(d6), .Data7(d7), .CLK4(c4), .CLK5(c5), .CLK6(c6), .CLK7(c7),
    .Q00(sram_8b_1_q00), .Q1(sram_8b_1_q1), .Q10(sram_8b_1_q10), .Q9(sram_8b_1_q9), .Q01(sram_8b_1_q01),
    .Q2(sram_8b_1_q2), .Q11(sram_8b_1_q11), .Q10_2(sram_8b_1_q10_2), .Q20(sram_8b_1_q20),
    .Q17(sram_8b_1_q17), .Q30(sram_8b_1_q30), .Q25(sram_8b_1_q25), .Q21(sram_8b_1_q21), .Q18(sram_8b_1_q18),
    .Q31(sram_8b_1_q31), .Q26(sram_8b_1_q26), .Q02(sram_8b_1_q02), .Q3(sram_8b_1_q3), .Q12(sram_8b_1_q12),
    .Q11_2(sram_8b_1_q11_2), .Q03(sram_8b_1_q03), .Q4(sram_8b_1_q4), .Q13(sram_8b_1_q13),
    .Q12_2(sram_8b_1_q12_2), .Q22(sram_8b_1_q22), .Q19(sram_8b_1_q19), .Q32(sram_8b_1_q32),
    .Q27(sram_8b_1_q27), .Q23(sram_8b_1_q23), .Q20_2(sram_8b_1_q20_2), .Q33(sram_8b_1_q33),
    .Q28(sram_8b_1_q28), .Q04(sram_8b_1_q04), .Q5(sram_8b_1_q5), .Q14(sram_8b_1_q14),
    .Q13_2(sram_8b_1_q13_2), .Q05(sram_8b_1_q05), .Q6(sram_8b_1_q6), .Q15(sram_8b_1_q15),
    .Q14_2(sram_8b_1_q14_2), .Q24(sram_8b_1_q24), .Q21_2(sram_8b_1_q21_2), .Q34(sram_8b_1_q34),
    .Q29(sram_8b_1_q29), .Q25_2(sram_8b_1_q25_2), .Q22_2(sram_8b_1_q22_2), .Q35(sram_8b_1_q35),
    .Q30_2(sram_8b_1_q30_2), .Q06(sram_8b_1_q06), .Q7(sram_8b_1_q7), .Q16(sram_8b_1_q16),
    .Q15_2(sram_8b_1_q15_2), .Q07(sram_8b_1_q07), .Q8(sram_8b_1_q8), .Q17_2(sram_8b_1_q17_2),
    .Q16_2(sram_8b_1_q16_2), .Q26_2(sram_8b_1_q26_2), .Q23_2(sram_8b_1_q23_2), .Q36(sram_8b_1_q36),
    .Q31_2(sram_8b_1_q31_2), .Q27_2(sram_8b_1_q27_2), .Q24_2(sram_8b_1_q24_2), .Q37(sram_8b_1_q37),
    .Q32_2(sram_8b_1_q32_2), .Q40(sram_8b_1_q40), .Q33_2(sram_8b_1_q33_2), .Q50(sram_8b_1_q50),
    .Q41(sram_8b_1_q41), .Q41_2(sram_8b_1_q41_2), .Q34_2(sram_8b_1_q34_2), .Q51(sram_8b_1_q51),
    .Q42(sram_8b_1_q42), .Q60(sram_8b_1_q60), .Q49(sram_8b_1_q49), .Q70(sram_8b_1_q70), .Q57(sram_8b_1_q57),
    .Q61(sram_8b_1_q61), .Q50_2(sram_8b_1_q50_2), .Q71(sram_8b_1_q71), .Q58(sram_8b_1_q58),
    .Q42_2(sram_8b_1_q42_2), .Q35_2(sram_8b_1_q35_2), .Q52(sram_8b_1_q52), .Q43(sram_8b_1_q43),
    .Q43_2(sram_8b_1_q43_2), .Q36_2(sram_8b_1_q36_2), .Q53(sram_8b_1_q53), .Q44(sram_8b_1_q44),
    .Q62(sram_8b_1_q62), .Q51_2(sram_8b_1_q51_2), .Q72(sram_8b_1_q72), .Q59(sram_8b_1_q59),
    .Q63(sram_8b_1_q63), .Q52_2(sram_8b_1_q52_2), .Q73(sram_8b_1_q73), .Q60_2(sram_8b_1_q60_2),
    .Q44_2(sram_8b_1_q44_2), .Q37_2(sram_8b_1_q37_2), .Q54(sram_8b_1_q54), .Q45(sram_8b_1_q45),
    .Q45_2(sram_8b_1_q45_2), .Q38(sram_8b_1_q38), .Q55(sram_8b_1_q55), .Q46(sram_8b_1_q46),
    .Q64(sram_8b_1_q64), .Q53_2(sram_8b_1_q53_2), .Q74(sram_8b_1_q74), .Q61_2(sram_8b_1_q61_2),
    .Q65(sram_8b_1_q65), .Q54_2(sram_8b_1_q54_2), .Q75(sram_8b_1_q75), .Q62_2(sram_8b_1_q62_2),
    .Q46_2(sram_8b_1_q46_2), .Q39(sram_8b_1_q39), .Q56(sram_8b_1_q56), .Q47(sram_8b_1_q47),
    .Q47_2(sram_8b_1_q47_2), .Q40_2(sram_8b_1_q40_2), .Q57_2(sram_8b_1_q57_2), .Q48(sram_8b_1_q48),
    .Q66(sram_8b_1_q66), .Q55_2(sram_8b_1_q55_2), .Q76(sram_8b_1_q76), .Q63_2(sram_8b_1_q63_2),
    .Q67(sram_8b_1_q67), .Q56_2(sram_8b_1_q56_2), .Q77(sram_8b_1_q77));  // open: Q64_2
  nand nand_1 (nand_1_out, sram_8b_1_q17, sram_8b_1_q10_2, sram_8b_1_q2, sram_8b_1_q9, sram_8b_1_q1);
  nand nand_2 (nand_2_out, nand_7_out, nand_6_out, nand_4_out, nand_3_out, nand_1_out);
  nand nand_3 (nand_3_out, sram_8b_1_q11_2, sram_8b_1_q3, sram_8b_1_q26, sram_8b_1_q18, sram_8b_1_q25);
  nand nand_4 (nand_4_out, sram_8b_1_q20_2, sram_8b_1_q27, sram_8b_1_q19, sram_8b_1_q12_2, sram_8b_1_q4);
  nand nand_5 (out_17, nand_15_out, nand_10_out, nand_2_out);
  nand nand_6 (nand_6_out, sram_8b_1_q14_2, sram_8b_1_q6, sram_8b_1_q13_2, sram_8b_1_q5, sram_8b_1_q28);
  nand nand_7 (nand_7_out, sram_8b_1_q7, sram_8b_1_q30_2, sram_8b_1_q22_2, sram_8b_1_q29, sram_8b_1_q21_2);
  nand nand_8 (nand_8_out, sram_8b_1_q31_2, sram_8b_1_q23_2, sram_8b_1_q16_2, sram_8b_1_q8, sram_8b_1_q15_2);
  nand nand_9 (nand_9_out, sram_8b_1_q34_2, sram_8b_1_q41, sram_8b_1_q33_2, sram_8b_1_q32_2, sram_8b_1_q24_2);
  nand nand_10 (nand_10_out, nand_13_out, nand_12_out, nand_11_out, nand_9_out, nand_8_out);
  nand nand_11 (nand_11_out, sram_8b_1_q58, sram_8b_1_q50_2, sram_8b_1_q57, sram_8b_1_q49, sram_8b_1_q42);
  nand nand_12 (nand_12_out, sram_8b_1_q51_2, sram_8b_1_q44, sram_8b_1_q36_2, sram_8b_1_q43, sram_8b_1_q35_2);
  nand nand_13 (nand_13_out, sram_8b_1_q45, sram_8b_1_q37_2, sram_8b_1_q60_2, sram_8b_1_q52_2, sram_8b_1_q59);
  nand nand_14 (nand_14_out, sram_8b_1_q54_2, sram_8b_1_q61_2, sram_8b_1_q53_2, sram_8b_1_q46, sram_8b_1_q38);
  nand nand_15 (nand_15_out, nand_17_out, nand_17_out, nand_17_out, nand_16_out, nand_14_out);
  nand nand_16 (nand_16_out, sram_8b_1_q48, sram_8b_1_q40_2, sram_8b_1_q47, sram_8b_1_q39, sram_8b_1_q62_2);
  nand nand_17 (nand_17_out, sram_8b_1_q56_2, sram_8b_1_q56_2, sram_8b_1_q56_2, sram_8b_1_q63_2, sram_8b_1_q55_2);
  LED led_1 (.in(sram_8b_1_q00));
  LED led_2 (.in(sram_8b_1_q10));
  LED led_3 (.in(sram_8b_1_q20));
  LED led_4 (.in(sram_8b_1_q30));
  LED led_5 (.in(sram_8b_1_q40));
  LED led_6 (.in(sram_8b_1_q50));
  LED led_7 (.in(sram_8b_1_q60));
  LED led_8 (.in(sram_8b_1_q70));
  LED led_9 (.in(sram_8b_1_q01));
  LED led_10 (.in(sram_8b_1_q02));
  LED led_11 (.in(sram_8b_1_q11));
  LED led_12 (.in(sram_8b_1_q12));
  LED led_13 (.in(sram_8b_1_q21));
  LED led_14 (.in(sram_8b_1_q22));
  LED led_15 (.in(sram_8b_1_q31));
  LED led_16 (.in(sram_8b_1_q32));
  LED led_17 (.in(sram_8b_1_q41_2));
  LED led_18 (.in(sram_8b_1_q42_2));
  LED led_19 (.in(sram_8b_1_q51));
  LED led_20 (.in(sram_8b_1_q52));
  LED led_21 (.in(sram_8b_1_q61));
  LED led_22 (.in(sram_8b_1_q62));
  LED led_23 (.in(sram_8b_1_q71));
  LED led_24 (.in(sram_8b_1_q72));
  LED led_25 (.in(sram_8b_1_q03));
  LED led_26 (.in(sram_8b_1_q13));
  LED led_27 (.in(sram_8b_1_q23));
  LED led_28 (.in(sram_8b_1_q33));
  LED led_29 (.in(sram_8b_1_q43_2));
  LED led_30 (.in(sram_8b_1_q53));
  LED led_31 (.in(sram_8b_1_q63));
  LED led_32 (.in(sram_8b_1_q73));
  LED led_33 (.in(sram_8b_1_q04));
  LED led_34 (.in(sram_8b_1_q14));
  LED led_35 (.in(sram_8b_1_q24));
  LED led_36 (.in(sram_8b_1_q34));
  LED led_37 (.in(sram_8b_1_q44_2));
  LED led_38 (.in(sram_8b_1_q54));
  LED led_39 (.in(sram_8b_1_q64));
  LED led_40 (.in(sram_8b_1_q74));
  LED led_41 (.in(sram_8b_1_q05));
  LED led_42 (.in(sram_8b_1_q06));
  LED led_43 (.in(sram_8b_1_q15));
  LED led_44 (.in(sram_8b_1_q16));
  LED led_45 (.in(sram_8b_1_q25_2));
  LED led_46 (.in(sram_8b_1_q26_2));
  LED led_47 (.in(sram_8b_1_q35));
  LED led_48 (.in(sram_8b_1_q36));
  LED led_49 (.in(sram_8b_1_q45_2));
  LED led_50 (.in(sram_8b_1_q46_2));
  LED led_51 (.in(sram_8b_1_q55));
  LED led_52 (.in(sram_8b_1_q56));
  LED led_53 (.in(sram_8b_1_q65));
  LED led_54 (.in(sram_8b_1_q66));
  LED led_55 (.in(sram_8b_1_q75));
  LED led_56 (.in(sram_8b_1_q76));
  LED led_57 (.in(sram_8b_1_q07));
  LED led_58 (.in(sram_8b_1_q17_2));
  LED led_59 (.in(sram_8b_1_q27_2));
  LED led_60 (.in(sram_8b_1_q37));
  LED led_61 (.in(sram_8b_1_q47_2));
  LED led_62 (.in(sram_8b_1_q57_2));
  LED led_63 (.in(sram_8b_1_q67));
  LED led_64 (.in(sram_8b_1_q77));
  not not_1 (not_1_out, Data0);
  not not_2 (not_2_out, Q00);
  not not_3 (not_3_out, Q10);
  not not_4 (not_4_out, Q20);
  not not_5 (not_5_out, Q30);
  not not_6 (not_6_out, Q40);
  not not_7 (not_7_out, Q50);
  not not_8 (not_8_out, Q60);
  nand nand_18 (nand_18_out, Data0, CLK0);
  nand nand_19 (nand_19_out, not_1_out, CLK0);
  nand nand_20 (nand_20_out, Q00, CLK1);
  nand nand_21 (nand_21_out, not_2_out, CLK1);
  nand nand_22 (nand_22_out, Q10, CLK2);
  nand nand_23 (nand_23_out, not_3_out, CLK2);
  nand nand_24 (nand_24_out, Q20, CLK3);
  nand nand_25 (nand_25_out, not_4_out, CLK3);
  nand nand_26 (nand_26_out, Q30, CLK4);
  nand nand_27 (nand_27_out, not_5_out, CLK4);
  nand nand_28 (nand_28_out, Q40, CLK5);
  nand nand_29 (nand_29_out, not_6_out, CLK5);
  nand nand_30 (nand_30_out, Q50, CLK6);
  nand nand_31 (nand_31_out, not_7_out, CLK6);
  nand nand_32 (nand_32_out, Q60, CLK7);
  nand nand_33 (nand_33_out, not_8_out, CLK7);
  nand nand_34 (Q00, nand_18_out, Q1);
  nand nand_35 (Q1, Q00, nand_19_out);
  nand nand_36 (Q10, nand_20_out, Q9);
  nand nand_37 (Q9, Q10, nand_21_out);
  nand nand_38 (Q20, nand_22_out, Q17);
  nand nand_39 (Q17, Q20, nand_23_out);
  nand nand_40 (Q30, nand_24_out, Q25);
  nand nand_41 (Q25, Q30, nand_25_out);
  nand nand_42 (Q40, nand_26_out, Q33_2);
  nand nand_43 (Q33_2, Q40, nand_27_out);
  nand nand_44 (Q50, nand_28_out, Q41);
  nand nand_45 (Q41, Q50, nand_29_out);
  nand nand_46 (Q60, nand_30_out, Q49);
  nand nand_47 (Q49, Q60, nand_31_out);
  nand nand_48 (Q70, nand_32_out, Q57);
  nand nand_49 (Q57, Q70, nand_33_out);
  not not_9 (not_9_out, Data1);
  not not_10 (not_10_out, Q01);
  not not_11 (not_11_out, Q11);
  not not_12 (not_12_out, Q21);
  not not_13 (not_13_out, Q31);
  not not_14 (not_14_out, Q41_2);
  not not_15 (not_15_out, Q51);
  not not_16 (not_16_out, Q61);
  nand nand_50 (nand_50_out, Data1, CLK0);
  nand nand_51 (nand_51_out, not_9_out, CLK0);
  nand nand_52 (nand_52_out, Q01, CLK1);
  nand nand_53 (nand_53_out, not_10_out, CLK1);
  nand nand_54 (nand_54_out, Q11, CLK2);
  nand nand_55 (nand_55_out, not_11_out, CLK2);
  nand nand_56 (nand_56_out, Q21, CLK3);
  nand nand_57 (nand_57_out, not_12_out, CLK3);
  nand nand_58 (nand_58_out, Q31, CLK4);
  nand nand_59 (nand_59_out, not_13_out, CLK4);
  nand nand_60 (nand_60_out, Q41_2, CLK5);
  nand nand_61 (nand_61_out, not_14_out, CLK5);
  nand nand_62 (nand_62_out, Q51, CLK6);
  nand nand_63 (nand_63_out, not_15_out, CLK6);
  nand nand_64 (nand_64_out, Q61, CLK7);
  nand nand_65 (nand_65_out, not_16_out, CLK7);
  nand nand_66 (Q01, nand_50_out, Q2);
  nand nand_67 (Q2, Q01, nand_51_out);
  nand nand_68 (Q11, nand_52_out, Q10_2);
  nand nand_69 (Q10_2, Q11, nand_53_out);
  nand nand_70 (Q21, nand_54_out, Q18);
  nand nand_71 (Q18, Q21, nand_55_out);
  nand nand_72 (Q31, nand_56_out, Q26);
  nand nand_73 (Q26, Q31, nand_57_out);
  nand nand_74 (Q41_2, nand_58_out, Q34_2);
  nand nand_75 (Q34_2, Q41_2, nand_59_out);
  nand nand_76 (Q51, nand_60_out, Q42);
  nand nand_77 (Q42, Q51, nand_61_out);
  nand nand_78 (Q61, nand_62_out, Q50_2);
  nand nand_79 (Q50_2, Q61, nand_63_out);
  nand nand_80 (Q71, nand_64_out, Q58);
  nand nand_81 (Q58, Q71, nand_65_out);
  not not_17 (not_17_out, Data2);
  not not_18 (not_18_out, Q02);
  not not_19 (not_19_out, Q12);
  not not_20 (not_20_out, Q22);
  not not_21 (not_21_out, Q32);
  not not_22 (not_22_out, Q42_2);
  not not_23 (not_23_out, Q52);
  not not_24 (not_24_out, Q62);
  nand nand_82 (nand_82_out, Data2, CLK0);
  nand nand_83 (nand_83_out, not_17_out, CLK0);
  nand nand_84 (nand_84_out, Q02, CLK1);
  nand nand_85 (nand_85_out, not_18_out, CLK1);
  nand nand_86 (nand_86_out, Q12, CLK2);
  nand nand_87 (nand_87_out, not_19_out, CLK2);
  nand nand_88 (nand_88_out, Q22, CLK3);
  nand nand_89 (nand_89_out, not_20_out, CLK3);
  nand nand_90 (nand_90_out, Q32, CLK4);
  nand nand_91 (nand_91_out, not_21_out, CLK4);
  nand nand_92 (nand_92_out, Q42_2, CLK5);
  nand nand_93 (nand_93_out, not_22_out, CLK5);
  nand nand_94 (nand_94_out, Q52, CLK6);
  nand nand_95 (nand_95_out, not_23_out, CLK6);
  nand nand_96 (nand_96_out, Q62, CLK7);
  nand nand_97 (nand_97_out, not_24_out, CLK7);
  nand nand_98 (Q02, nand_82_out, Q3);
  nand nand_99 (Q3, Q02, nand_83_out);
  nand nand_100 (Q12, nand_84_out, Q11_2);
  nand nand_101 (Q11_2, Q12, nand_85_out);
  nand nand_102 (Q22, nand_86_out, Q19);
  nand nand_103 (Q19, Q22, nand_87_out);
  nand nand_104 (Q32, nand_88_out, Q27);
  nand nand_105 (Q27, Q32, nand_89_out);
  nand nand_106 (Q42_2, nand_90_out, Q35_2);
  nand nand_107 (Q35_2, Q42_2, nand_91_out);
  nand nand_108 (Q52, nand_92_out, Q43);
  nand nand_109 (Q43, Q52, nand_93_out);
  nand nand_110 (Q62, nand_94_out, Q51_2);
  nand nand_111 (Q51_2, Q62, nand_95_out);
  nand nand_112 (Q72, nand_96_out, Q59);
  nand nand_113 (Q59, Q72, nand_97_out);
  not not_25 (not_25_out, Data3);
  not not_26 (not_26_out, Q03);
  not not_27 (not_27_out, Q13);
  not not_28 (not_28_out, Q23);
  not not_29 (not_29_out, Q33);
  not not_30 (not_30_out, Q43_2);
  not not_31 (not_31_out, Q53);
  not not_32 (not_32_out, Q63);
  nand nand_114 (nand_114_out, Data3, CLK0);
  nand nand_115 (nand_115_out, not_25_out, CLK0);
  nand nand_116 (nand_116_out, Q03, CLK1);
  nand nand_117 (nand_117_out, not_26_out, CLK1);
  nand nand_118 (nand_118_out, Q13, CLK2);
  nand nand_119 (nand_119_out, not_27_out, CLK2);
  nand nand_120 (nand_120_out, Q23, CLK3);
  nand nand_121 (nand_121_out, not_28_out, CLK3);
  nand nand_122 (nand_122_out, Q33, CLK4);
  nand nand_123 (nand_123_out, not_29_out, CLK4);
  nand nand_124 (nand_124_out, Q43_2, CLK5);
  nand nand_125 (nand_125_out, not_30_out, CLK5);
  nand nand_126 (nand_126_out, Q53, CLK6);
  nand nand_127 (nand_127_out, not_31_out, CLK6);
  nand nand_128 (nand_128_out, Q63, CLK7);
  nand nand_129 (nand_129_out, not_32_out, CLK7);
  nand nand_130 (Q03, nand_114_out, Q4);
  nand nand_131 (Q4, Q03, nand_115_out);
  nand nand_132 (Q13, nand_116_out, Q12_2);
  nand nand_133 (Q12_2, Q13, nand_117_out);
  nand nand_134 (Q23, nand_118_out, Q20_2);
  nand nand_135 (Q20_2, Q23, nand_119_out);
  nand nand_136 (Q33, nand_120_out, Q28);
  nand nand_137 (Q28, Q33, nand_121_out);
  nand nand_138 (Q43_2, nand_122_out, Q36_2);
  nand nand_139 (Q36_2, Q43_2, nand_123_out);
  nand nand_140 (Q53, nand_124_out, Q44);
  nand nand_141 (Q44, Q53, nand_125_out);
  nand nand_142 (Q63, nand_126_out, Q52_2);
  nand nand_143 (Q52_2, Q63, nand_127_out);
  nand nand_144 (Q73, nand_128_out, Q60_2);
  nand nand_145 (Q60_2, Q73, nand_129_out);
  not not_33 (not_33_out, Data4);
  not not_34 (not_34_out, Q04);
  not not_35 (not_35_out, Q14);
  not not_36 (not_36_out, Q24);
  not not_37 (not_37_out, Q34);
  not not_38 (not_38_out, Q44_2);
  not not_39 (not_39_out, Q54);
  not not_40 (not_40_out, Q64);
  nand nand_146 (nand_146_out, Data4, CLK0);
  nand nand_147 (nand_147_out, not_33_out, CLK0);
  nand nand_148 (nand_148_out, Q04, CLK1);
  nand nand_149 (nand_149_out, not_34_out, CLK1);
  nand nand_150 (nand_150_out, Q14, CLK2);
  nand nand_151 (nand_151_out, not_35_out, CLK2);
  nand nand_152 (nand_152_out, Q24, CLK3);
  nand nand_153 (nand_153_out, not_36_out, CLK3);
  nand nand_154 (nand_154_out, Q34, CLK4);
  nand nand_155 (nand_155_out, not_37_out, CLK4);
  nand nand_156 (nand_156_out, Q44_2, CLK5);
  nand nand_157 (nand_157_out, not_38_out, CLK5);
  nand nand_158 (nand_158_out, Q54, CLK6);
  nand nand_159 (nand_159_out, not_39_out, CLK6);
  nand nand_160 (nand_160_out, Q64, CLK7);
  nand nand_161 (nand_161_out, not_40_out, CLK7);
  nand nand_162 (Q04, nand_146_out, Q5);
  nand nand_163 (Q5, Q04, nand_147_out);
  nand nand_164 (Q14, nand_148_out, Q13_2);
  nand nand_165 (Q13_2, Q14, nand_149_out);
  nand nand_166 (Q24, nand_150_out, Q21_2);
  nand nand_167 (Q21_2, Q24, nand_151_out);
  nand nand_168 (Q34, nand_152_out, Q29);
  nand nand_169 (Q29, Q34, nand_153_out);
  nand nand_170 (Q44_2, nand_154_out, Q37_2);
  nand nand_171 (Q37_2, Q44_2, nand_155_out);
  nand nand_172 (Q54, nand_156_out, Q45);
  nand nand_173 (Q45, Q54, nand_157_out);
  nand nand_174 (Q64, nand_158_out, Q53_2);
  nand nand_175 (Q53_2, Q64, nand_159_out);
  nand nand_176 (Q74, nand_160_out, Q61_2);
  nand nand_177 (Q61_2, Q74, nand_161_out);
  not not_41 (not_41_out, Data5);
  not not_42 (not_42_out, Q05);
  not not_43 (not_43_out, Q15);
  not not_44 (not_44_out, Q25_2);
  not not_45 (not_45_out, Q35);
  not not_46 (not_46_out, Q45_2);
  not not_47 (not_47_out, Q55);
  not not_48 (not_48_out, Q65);
  nand nand_178 (nand_178_out, Data5, CLK0);
  nand nand_179 (nand_179_out, not_41_out, CLK0);
  nand nand_180 (nand_180_out, Q05, CLK1);
  nand nand_181 (nand_181_out, not_42_out, CLK1);
  nand nand_182 (nand_182_out, Q15, CLK2);
  nand nand_183 (nand_183_out, not_43_out, CLK2);
  nand nand_184 (nand_184_out, Q25_2, CLK3);
  nand nand_185 (nand_185_out, not_44_out, CLK3);
  nand nand_186 (nand_186_out, Q35, CLK4);
  nand nand_187 (nand_187_out, not_45_out, CLK4);
  nand nand_188 (nand_188_out, Q45_2, CLK5);
  nand nand_189 (nand_189_out, not_46_out, CLK5);
  nand nand_190 (nand_190_out, Q55, CLK6);
  nand nand_191 (nand_191_out, not_47_out, CLK6);
  nand nand_192 (nand_192_out, Q65, CLK7);
  nand nand_193 (nand_193_out, not_48_out, CLK7);
  nand nand_194 (Q05, nand_178_out, Q6);
  nand nand_195 (Q6, Q05, nand_179_out);
  nand nand_196 (Q15, nand_180_out, Q14_2);
  nand nand_197 (Q14_2, Q15, nand_181_out);
  nand nand_198 (Q25_2, nand_182_out, Q22_2);
  nand nand_199 (Q22_2, Q25_2, nand_183_out);
  nand nand_200 (Q35, nand_184_out, Q30_2);
  nand nand_201 (Q30_2, Q35, nand_185_out);
  nand nand_202 (Q45_2, nand_186_out, Q38);
  nand nand_203 (Q38, Q45_2, nand_187_out);
  nand nand_204 (Q55, nand_188_out, Q46);
  nand nand_205 (Q46, Q55, nand_189_out);
  nand nand_206 (Q65, nand_190_out, Q54_2);
  nand nand_207 (Q54_2, Q65, nand_191_out);
  nand nand_208 (Q75, nand_192_out, Q62_2);
  nand nand_209 (Q62_2, Q75, nand_193_out);
  not not_49 (not_49_out, Data6);
  not not_50 (not_50_out, Q06);
  not not_51 (not_51_out, Q16);
  not not_52 (not_52_out, Q26_2);
  not not_53 (not_53_out, Q36);
  not not_54 (not_54_out, Q46_2);
  not not_55 (not_55_out, Q56);
  not not_56 (not_56_out, Q66);
  nand nand_210 (nand_210_out, Data6, CLK0);
  nand nand_211 (nand_211_out, not_49_out, CLK0);
  nand nand_212 (nand_212_out, Q06, CLK1);
  nand nand_213 (nand_213_out, not_50_out, CLK1);
  nand nand_214 (nand_214_out, Q16, CLK2);
  nand nand_215 (nand_215_out, not_51_out, CLK2);
  nand nand_216 (nand_216_out, Q26_2, CLK3);
  nand nand_217 (nand_217_out, not_52_out, CLK3);
  nand nand_218 (nand_218_out, Q36, CLK4);
  nand nand_219 (nand_219_out, not_53_out, CLK4);
  nand nand_220 (nand_220_out, Q46_2, CLK5);
  nand nand_221 (nand_221_out, not_54_out, CLK5);
  nand nand_222 (nand_222_out, Q56, CLK6);
  nand nand_223 (nand_223_out, not_55_out, CLK6);
  nand nand_224 (nand_224_out, Q66, CLK7);
  nand nand_225 (nand_225_out, not_56_out, CLK7);
  nand nand_226 (Q06, nand_210_out, Q7);
  nand nand_227 (Q7, Q06, nand_211_out);
  nand nand_228 (Q16, nand_212_out, Q15_2);
  nand nand_229 (Q15_2, Q16, nand_213_out);
  nand nand_230 (Q26_2, nand_214_out, Q23_2);
  nand nand_231 (Q23_2, Q26_2, nand_215_out);
  nand nand_232 (Q36, nand_216_out, Q31_2);
  nand nand_233 (Q31_2, Q36, nand_217_out);
  nand nand_234 (Q46_2, nand_218_out, Q39);
  nand nand_235 (Q39, Q46_2, nand_219_out);
  nand nand_236 (Q56, nand_220_out, Q47);
  nand nand_237 (Q47, Q56, nand_221_out);
  nand nand_238 (Q66, nand_222_out, Q55_2);
  nand nand_239 (Q55_2, Q66, nand_223_out);
  nand nand_240 (Q76, nand_224_out, Q63_2);
  nand nand_241 (Q63_2, Q76, nand_225_out);
  not not_57 (not_57_out, Data7);
  not not_58 (not_58_out, Q07);
  not not_59 (not_59_out, Q17_2);
  not not_60 (not_60_out, Q27_2);
  not not_61 (not_61_out, Q37);
  not not_62 (not_62_out, Q47_2);
  not not_63 (not_63_out, Q57_2);
  not not_64 (not_64_out, Q67);
  nand nand_242 (nand_242_out, Data7, CLK0);
  nand nand_243 (nand_243_out, not_57_out, CLK0);
  nand nand_244 (nand_244_out, Q07, CLK1);
  nand nand_245 (nand_245_out, not_58_out, CLK1);
  nand nand_246 (nand_246_out, Q17_2, CLK2);
  nand nand_247 (nand_247_out, not_59_out, CLK2);
  nand nand_248 (nand_248_out, Q27_2, CLK3);
  nand nand_249 (nand_249_out, not_60_out, CLK3);
  nand nand_250 (nand_250_out, Q37, CLK4);
  nand nand_251 (nand_251_out, not_61_out, CLK4);
  nand nand_252 (nand_252_out, Q47_2, CLK5);
  nand nand_253 (nand_253_out, not_62_out, CLK5);
  nand nand_254 (nand_254_out, Q57_2, CLK6);
  nand nand_255 (nand_255_out, not_63_out, CLK6);
  nand nand_256 (nand_256_out, Q67, CLK7);
  nand nand_257 (nand_257_out, not_64_out, CLK7);
  nand nand_258 (Q07, nand_242_out, Q8);
  nand nand_259 (Q8, Q07, nand_243_out);
  nand nand_260 (Q17_2, nand_244_out, Q16_2);
  nand nand_261 (Q16_2, Q17_2, nand_245_out);
  nand nand_262 (Q27_2, nand_246_out, Q24_2);
  nand nand_263 (Q24_2, Q27_2, nand_247_out);
  nand nand_264 (Q37, nand_248_out, Q32_2);
  nand nand_265 (Q32_2, Q37, nand_249_out);
  nand nand_266 (Q47_2, nand_250_out, Q40_2);
  nand nand_267 (Q40_2, Q47_2, nand_251_out);
  nand nand_268 (Q57_2, nand_252_out, Q48);
  nand nand_269 (Q48, Q57_2, nand_253_out);
  nand nand_270 (Q67, nand_254_out, Q56_2);
  nand nand_271 (Q56_2, Q67, nand_255_out);
  nand nand_272 (Q77, nand_256_out, Q64_2);
  nand nand_273 (Q64_2, Q77, nand_257_out);
endmodule
