// Digital circuit SRAM_8b.dig as structural Verilog
module SRAM_8b (
  input  Data0,
  input  CLK0,
  input  CLK1,
  input  Data1,
  input  CLK2,
  input  CLK3,
  input  Data2,
  input  Data3,
  input  Data4,
  input  Data5,
  input  Data6,
  input  Data7,
  input  CLK4,
  input  CLK5,
  input  CLK6,
  input  CLK7,
  output Q00,
  output Q1,
  output Q10,
  output Q9,
  output Q01,
  output Q2,
  output Q11,
  output Q10_2,
  output Q20,
  output Q17,
  output Q30,
  output Q25,
  output Q21,
  output Q18,
  output Q31,
  output Q26,
  output Q02,
  output Q3,
  output Q12,
  output Q11_2,
  output Q03,
  output Q4,
  output Q13,
  output Q12_2,
  output Q22,
  output Q19,
  output Q32,
  output Q27,
  output Q23,
  output Q20_2,
  output Q33,
  output Q28,
  output Q04,
  output Q5,
  output Q14,
  output Q13_2,
  output Q05,
  output Q6,
  output Q15,
  output Q14_2,
  output Q24,
  output Q21_2,
  output Q34,
  output Q29,
  output Q25_2,
  output Q22_2,
  output Q35,
  output Q30_2,
  output Q06,
  output Q7,
  output Q16,
  output Q15_2,
  output Q07,
  output Q8,
  output Q17_2,
  output Q16_2,
  output Q26_2,
  output Q23_2,
  output Q36,
  output Q31_2,
  output Q27_2,
  output Q24_2,
  output Q37,
  output Q32_2,
  output Q40,
  output Q33_2,
  output Q50,
  output Q41,
  output Q41_2,
  output Q34_2,
  output Q51,
  output Q42,
  output Q60,
  output Q49,
  output Q70,
  output Q57,
  output Q61,
  output Q50_2,
  output Q71,
  output Q58,
  output Q42_2,
  output Q35_2,
  output Q52,
  output Q43,
  output Q43_2,
  output Q36_2,
  output Q53,
  output Q44,
  output Q62,
  output Q51_2,
  output Q72,
  output Q59,
  output Q63,
  output Q52_2,
  output Q73,
  output Q60_2,
  output Q44_2,
  output Q37_2,
  output Q54,
  output Q45,
  output Q45_2,
  output Q38,
  output Q55,
  output Q46,
  output Q64,
  output Q53_2,
  output Q74,
  output Q61_2,
  output Q65,
  output Q54_2,
  output Q75,
  output Q62_2,
  output Q46_2,
  output Q39,
  output Q56,
  output Q47,
  output Q47_2,
  output Q40_2,
  output Q57_2,
  output Q48,
  output Q66,
  output Q55_2,
  output Q76,
  output Q63_2,
  output Q67,
  output Q56_2,
  output Q77,
  output Q64_2
);

  wire nand_1_out, nand_2_out, nand_3_out, nand_4_out, nand_5_out, nand_6_out, nand_7_out, nand_8_out,
       nand_9_out, nand_10_out, nand_11_out, nand_12_out, nand_13_out, nand_14_out, nand_15_out, nand_16_out,
       nand_33_out, nand_34_out, nand_35_out, nand_36_out, nand_37_out, nand_38_out, nand_39_out,
       nand_40_out, nand_41_out, nand_42_out, nand_43_out, nand_44_out, nand_45_out, nand_46_out,
       nand_47_out, nand_48_out, nand_65_out, nand_66_out, nand_67_out, nand_68_out, nand_69_out,
       nand_70_out, nand_71_out, nand_72_out, nand_73_out, nand_74_out, nand_75_out, nand_76_out,
       nand_77_out, nand_78_out, nand_79_out, nand_80_out, nand_97_out, nand_98_out, nand_99_out,
       nand_100_out, nand_101_out, nand_102_out, nand_103_out, nand_104_out, nand_105_out, nand_106_out,
       nand_107_out, nand_108_out, nand_109_out, nand_110_out, nand_111_out, nand_112_out, nand_129_out,
       nand_130_out, nand_131_out, nand_132_out, nand_133_out, nand_134_out, nand_135_out, nand_136_out,
       nand_137_out, nand_138_out, nand_139_out, nand_140_out, nand_141_out, nand_142_out, nand_143_out,
       nand_144_out, nand_161_out, nand_162_out, nand_163_out, nand_164_out, nand_165_out, nand_166_out,
       nand_167_out, nand_168_out, nand_169_out, nand_170_out, nand_171_out, nand_172_out, nand_173_out,
       nand_174_out, nand_175_out, nand_176_out, nand_193_out, nand_194_out, nand_195_out, nand_196_out,
       nand_197_out, nand_198_out, nand_199_out, nand_200_out, nand_201_out, nand_202_out, nand_203_out,
       nand_204_out, nand_205_out, nand_206_out, nand_207_out, nand_208_out, nand_225_out, nand_226_out,
       nand_227_out, nand_228_out, nand_229_out, nand_230_out, nand_231_out, nand_232_out, nand_233_out,
       nand_234_out, nand_235_out, nand_236_out, nand_237_out, nand_238_out, nand_239_out, nand_240_out,
       not_1_out, not_2_out, not_3_out, not_4_out, not_5_out, not_6_out, not_7_out, not_8_out, not_9_out,
       not_10_out, not_11_out, not_12_out, not_13_out, not_14_out, not_15_out, not_16_out, not_17_out,
       not_18_out, not_19_out, not_20_out, not_21_out, not_22_out, not_23_out, not_24_out, not_25_out,
       not_26_out, not_27_out, not_28_out, not_29_out, not_30_out, not_31_out, not_32_out, not_33_out,
       not_34_out, not_35_out, not_36_out, not_37_out, not_38_out, not_39_out, not_40_out, not_41_out,
       not_42_out, not_43_out, not_44_out, not_45_out, not_46_out, not_47_out, not_48_out, not_49_out,
       not_50_out, not_51_out, not_52_out, not_53_out, not_54_out, not_55_out, not_56_out, not_57_out,
       not_58_out, not_59_out, not_60_out, not_61_out, not_62_out, not_63_out, not_64_out;

  not not_1 (not_1_out, Data0);
  not not_2 (not_2_out, Q00);
  not not_3 (not_3_out, Q10);
  not not_4 (not_4_out, Q20);
  not not_5 (not_5_out, Q30);
  not not_6 (not_6_out, Q40);
  not not_7 (not_7_out, Q50);
  not not_8 (not_8_out, Q60);
  nand nand_1 (nand_1_out, Data0, CLK0);
  nand nand_2 (nand_2_out, not_1_out, CLK0);
  nand nand_3 (nand_3_out, Q00, CLK1);
  nand nand_4 (nand_4_out, not_2_out, CLK1);
  nand nand_5 (nand_5_out, Q10, CLK2);
  nand nand_6 (nand_6_out, not_3_out, CLK2);
  nand nand_7 (nand_7_out, Q20, CLK3);
  nand nand_8 (nand_8_out, not_4_out, CLK3);
  nand nand_9 (nand_9_out, Q30, CLK4);
  nand nand_10 (nand_10_out, not_5_out, CLK4);
  nand nand_11 (nand_11_out, Q40, CLK5);
  nand nand_12 (nand_12_out, not_6_out, CLK5);
  nand nand_13 (nand_13_out, Q50, CLK6);
  nand nand_14 (nand_14_out, not_7_out, CLK6);
  nand nand_15 (nand_15_out, Q60, CLK7);
  nand nand_16 (nand_16_out, not_8_out, CLK7);
  nand nand_17 (Q00, nand_1_out, Q1);
  nand nand_18 (Q1, Q00, nand_2_out);
  nand nand_19 (Q10, nand_3_out, Q9);
  nand nand_20 (Q9, Q10, nand_4_out);
  nand nand_21 (Q20, nand_5_out, Q17);
  nand nand_22 (Q17, Q20, nand_6_out);
  nand nand_23 (Q30, nand_7_out, Q25);
  nand nand_24 (Q25, Q30, nand_8_out);
  nand nand_25 (Q40, nand_9_out, Q33_2);
  nand nand_26 (Q33_2, Q40, nand_10_out);
  nand nand_27 (Q50, nand_11_out, Q41);
  nand nand_28 (Q41, Q50, nand_12_out);
  nand nand_29 (Q60, nand_13_out, Q49);
  nand nand_30 (Q49, Q60, nand_14_out);
  nand nand_31 (Q70, nand_15_out, Q57);
  nand nand_32 (Q57, Q70, nand_16_out);
  not not_9 (not_9_out, Data1);
  not not_10 (not_10_out, Q01);
  not not_11 (not_11_out, Q11);
  not not_12 (not_12_out, Q21);
  not not_13 (not_13_out, Q31);
  not not_14 (not_14_out, Q41_2);
  not not_15 (not_15_out, Q51);
  not not_16 (not_16_out, Q61);
  nand nand_33 (nand_33_out, Data1, CLK0);
  nand nand_34 (nand_34_out, not_9_out, CLK0);
  nand nand_35 (nand_35_out, Q01, CLK1);
  nand nand_36 (nand_36_out, not_10_out, CLK1);
  nand nand_37 (nand_37_out, Q11, CLK2);
  nand nand_38 (nand_38_out, not_11_out, CLK2);
  nand nand_39 (nand_39_out, Q21, CLK3);
  nand nand_40 (nand_40_out, not_12_out, CLK3);
  nand nand_41 (nand_41_out, Q31, CLK4);
  nand nand_42 (nand_42_out, not_13_out, CLK4);
  nand nand_43 (nand_43_out, Q41_2, CLK5);
  nand nand_44 (nand_44_out, not_14_out, CLK5);
  nand nand_45 (nand_45_out, Q51, CLK6);
  nand nand_46 (nand_46_out, not_15_out, CLK6);
  nand nand_47 (nand_47_out, Q61, CLK7);
  nand nand_48 (nand_48_out, not_16_out, CLK7);
  nand nand_49 (Q01, nand_33_out, Q2);
  nand nand_50 (Q2, Q01, nand_34_out);
  nand nand_51 (Q11, nand_35_out, Q10_2);
  nand nand_52 (Q10_2, Q11, nand_36_out);
  nand nand_53 (Q21, nand_37_out, Q18);
  nand nand_54 (Q18, Q21, nand_38_out);
  nand nand_55 (Q31, nand_39_out, Q26);
  nand nand_56 (Q26, Q31, nand_40_out);
  nand nand_57 (Q41_2, nand_41_out, Q34_2);
  nand nand_58 (Q34_2, Q41_2, nand_42_out);
  nand nand_59 (Q51, nand_43_out, Q42);
  nand nand_60 (Q42, Q51, nand_44_out);
  nand nand_61 (Q61, nand_45_out, Q50_2);
  nand nand_62 (Q50_2, Q61, nand_46_out);
  nand nand_63 (Q71, nand_47_out, Q58);
  nand nand_64 (Q58, Q71, nand_48_out);
  not not_17 (not_17_out, Data2);
  not not_18 (not_18_out, Q02);
  not not_19 (not_19_out, Q12);
  not not_20 (not_20_out, Q22);
  not not_21 (not_21_out, Q32);
  not not_22 (not_22_out, Q42_2);
  not not_23 (not_23_out, Q52);
  not not_24 (not_24_out, Q62);
  nand nand_65 (nand_65_out, Data2, CLK0);
  nand nand_66 (nand_66_out, not_17_out, CLK0);
  nand nand_67 (nand_67_out, Q02, CLK1);
  nand nand_68 (nand_68_out, not_18_out, CLK1);
  nand nand_69 (nand_69_out, Q12, CLK2);
  nand nand_70 (nand_70_out, not_19_out, CLK2);
  nand nand_71 (nand_71_out, Q22, CLK3);
  nand nand_72 (nand_72_out, not_20_out, CLK3);
  nand nand_73 (nand_73_out, Q32, CLK4);
  nand nand_74 (nand_74_out, not_21_out, CLK4);
  nand nand_75 (nand_75_out, Q42_2, CLK5);
  nand nand_76 (nand_76_out, not_22_out, CLK5);
  nand nand_77 (nand_77_out, Q52, CLK6);
  nand nand_78 (nand_78_out, not_23_out, CLK6);
  nand nand_79 (nand_79_out, Q62, CLK7);
  nand nand_80 (nand_80_out, not_24_out, CLK7);
  nand nand_81 (Q02, nand_65_out, Q3);
  nand nand_82 (Q3, Q02, nand_66_out);
  nand nand_83 (Q12, nand_67_out, Q11_2);
  nand nand_84 (Q11_2, Q12, nand_68_out);
  nand nand_85 (Q22, nand_69_out, Q19);
  nand nand_86 (Q19, Q22, nand_70_out);
  nand nand_87 (Q32, nand_71_out, Q27);
  nand nand_88 (Q27, Q32, nand_72_out);
  nand nand_89 (Q42_2, nand_73_out, Q35_2);
  nand nand_90 (Q35_2, Q42_2, nand_74_out);
  nand nand_91 (Q52, nand_75_out, Q43);
  nand nand_92 (Q43, Q52, nand_76_out);
  nand nand_93 (Q62, nand_77_out, Q51_2);
  nand nand_94 (Q51_2, Q62, nand_78_out);
  nand nand_95 (Q72, nand_79_out, Q59);
  nand nand_96 (Q59, Q72, nand_80_out);
  not not_25 (not_25_out, Data3);
  not not_26 (not_26_out, Q03);
  not not_27 (not_27_out, Q13);
  not not_28 (not_28_out, Q23);
  not not_29 (not_29_out, Q33);
  not not_30 (not_30_out, Q43_2);
  not not_31 (not_31_out, Q53);
  not not_32 (not_32_out, Q63);
  nand nand_97 (nand_97_out, Data3, CLK0);
  nand nand_98 (nand_98_out, not_25_out, CLK0);
  nand nand_99 (nand_99_out, Q03, CLK1);
  nand nand_100 (nand_100_out, not_26_out, CLK1);
  nand nand_101 (nand_101_out, Q13, CLK2);
  nand nand_102 (nand_102_out, not_27_out, CLK2);
  nand nand_103 (nand_103_out, Q23, CLK3);
  nand nand_104 (nand_104_out, not_28_out, CLK3);
  nand nand_105 (nand_105_out, Q33, CLK4);
  nand nand_106 (nand_106_out, not_29_out, CLK4);
  nand nand_107 (nand_107_out, Q43_2, CLK5);
  nand nand_108 (nand_108_out, not_30_out, CLK5);
  nand nand_109 (nand_109_out, Q53, CLK6);
  nand nand_110 (nand_110_out, not_31_out, CLK6);
  nand nand_111 (nand_111_out, Q63, CLK7);
  nand nand_112 (nand_112_out, not_32_out, CLK7);
  nand nand_113 (Q03, nand_97_out, Q4);
  nand nand_114 (Q4, Q03, nand_98_out);
  nand nand_115 (Q13, nand_99_out, Q12_2);
  nand nand_116 (Q12_2, Q13, nand_100_out);
  nand nand_117 (Q23, nand_101_out, Q20_2);
  nand nand_118 (Q20_2, Q23, nand_102_out);
  nand nand_119 (Q33, nand_103_out, Q28);
  nand nand_120 (Q28, Q33, nand_104_out);
  nand nand_121 (Q43_2, nand_105_out, Q36_2);
  nand nand_122 (Q36_2, Q43_2, nand_106_out);
  nand nand_123 (Q53, nand_107_out, Q44);
  nand nand_124 (Q44, Q53, nand_108_out);
  nand nand_125 (Q63, nand_109_out, Q52_2);
  nand nand_126 (Q52_2, Q63, nand_110_out);
  nand nand_127 (Q73, nand_111_out, Q60_2);
  nand nand_128 (Q60_2, Q73, nand_112_out);
  not not_33 (not_33_out, Data4);
  not not_34 (not_34_out, Q04);
  not not_35 (not_35_out, Q14);
  not not_36 (not_36_out, Q24);
  not not_37 (not_37_out, Q34);
  not not_38 (not_38_out, Q44_2);
  not not_39 (not_39_out, Q54);
  not not_40 (not_40_out, Q64);
  nand nand_129 (nand_129_out, Data4, CLK0);
  nand nand_130 (nand_130_out, not_33_out, CLK0);
  nand nand_131 (nand_131_out, Q04, CLK1);
  nand nand_132 (nand_132_out, not_34_out, CLK1);
  nand nand_133 (nand_133_out, Q14, CLK2);
  nand nand_134 (nand_134_out, not_35_out, CLK2);
  nand nand_135 (nand_135_out, Q24, CLK3);
  nand nand_136 (nand_136_out, not_36_out, CLK3);
  nand nand_137 (nand_137_out, Q34, CLK4);
  nand nand_138 (nand_138_out, not_37_out, CLK4);
  nand nand_139 (nand_139_out, Q44_2, CLK5);
  nand nand_140 (nand_140_out, not_38_out, CLK5);
  nand nand_141 (nand_141_out, Q54, CLK6);
  nand nand_142 (nand_142_out, not_39_out, CLK6);
  nand nand_143 (nand_143_out, Q64, CLK7);
  nand nand_144 (nand_144_out, not_40_out, CLK7);
  nand nand_145 (Q04, nand_129_out, Q5);
  nand nand_146 (Q5, Q04, nand_130_out);
  nand nand_147 (Q14, nand_131_out, Q13_2);
  nand nand_148 (Q13_2, Q14, nand_132_out);
  nand nand_149 (Q24, nand_133_out, Q21_2);
  nand nand_150 (Q21_2, Q24, nand_134_out);
  nand nand_151 (Q34, nand_135_out, Q29);
  nand nand_152 (Q29, Q34, nand_136_out);
  nand nand_153 (Q44_2, nand_137_out, Q37_2);
  nand nand_154 (Q37_2, Q44_2, nand_138_out);
  nand nand_155 (Q54, nand_139_out, Q45);
  nand nand_156 (Q45, Q54, nand_140_out);
  nand nand_157 (Q64, nand_141_out, Q53_2);
  nand nand_158 (Q53_2, Q64, nand_142_out);
  nand nand_159 (Q74, nand_143_out, Q61_2);
  nand nand_160 (Q61_2, Q74, nand_144_out);
  not not_41 (not_41_out, Data5);
  not not_42 (not_42_out, Q05);
  not not_43 (not_43_out, Q15);
  not not_44 (not_44_out, Q25_2);
  not not_45 (not_45_out, Q35);
  not not_46 (not_46_out, Q45_2);
  not not_47 (not_47_out, Q55);
  not not_48 (not_48_out, Q65);
  nand nand_161 (nand_161_out, Data5, CLK0);
  nand nand_162 (nand_162_out, not_41_out, CLK0);
  nand nand_163 (nand_163_out, Q05, CLK1);
  nand nand_164 (nand_164_out, not_42_out, CLK1);
  nand nand_165 (nand_165_out, Q15, CLK2);
  nand nand_166 (nand_166_out, not_43_out, CLK2);
  nand nand_167 (nand_167_out, Q25_2, CLK3);
  nand nand_168 (nand_168_out, not_44_out, CLK3);
  nand nand_169 (nand_169_out, Q35, CLK4);
  nand nand_170 (nand_170_out, not_45_out, CLK4);
  nand nand_171 (nand_171_out, Q45_2, CLK5);
  nand nand_172 (nand_172_out, not_46_out, CLK5);
  nand nand_173 (nand_173_out, Q55, CLK6);
  nand nand_174 (nand_174_out, not_47_out, CLK6);
  nand nand_175 (nand_175_out, Q65, CLK7);
  nand nand_176 (nand_176_out, not_48_out, CLK7);
  nand nand_177 (Q05, nand_161_out, Q6);
  nand nand_178 (Q6, Q05, nand_162_out);
  nand nand_179 (Q15, nand_163_out, Q14_2);
  nand nand_180 (Q14_2, Q15, nand_164_out);
  nand nand_181 (Q25_2, nand_165_out, Q22_2);
  nand nand_182 (Q22_2, Q25_2, nand_166_out);
  nand nand_183 (Q35, nand_167_out, Q30_2);
  nand nand_184 (Q30_2, Q35, nand_168_out);
  nand nand_185 (Q45_2, nand_169_out, Q38);
  nand nand_186 (Q38, Q45_2, nand_170_out);
  nand nand_187 (Q55, nand_171_out, Q46);
  nand nand_188 (Q46, Q55, nand_172_out);
  nand nand_189 (Q65, nand_173_out, Q54_2);
  nand nand_190 (Q54_2, Q65, nand_174_out);
  nand nand_191 (Q75, nand_175_out, Q62_2);
  nand nand_192 (Q62_2, Q75, nand_176_out);
  not not_49 (not_49_out, Data6);
  not not_50 (not_50_out, Q06);
  not not_51 (not_51_out, Q16);
  not not_52 (not_52_out, Q26_2);
  not not_53 (not_53_out, Q36);
  not not_54 (not_54_out, Q46_2);
  not not_55 (not_55_out, Q56);
  not not_56 (not_56_out, Q66);
  nand nand_193 (nand_193_out, Data6, CLK0);
  nand nand_194 (nand_194_out, not_49_out, CLK0);
  nand nand_195 (nand_195_out, Q06, CLK1);
  nand nand_196 (nand_196_out, not_50_out, CLK1);
  nand nand_197 (nand_197_out, Q16, CLK2);
  nand nand_198 (nand_198_out, not_51_out, CLK2);
  nand nand_199 (nand_199_out, Q26_2, CLK3);
  nand nand_200 (nand_200_out, not_52_out, CLK3);
  nand nand_201 (nand_201_out, Q36, CLK4);
  nand nand_202 (nand_202_out, not_53_out, CLK4);
  nand nand_203 (nand_203_out, Q46_2, CLK5);
  nand nand_204 (nand_204_out, not_54_out, CLK5);
  nand nand_205 (nand_205_out, Q56, CLK6);
  nand nand_206 (nand_206_out, not_55_out, CLK6);
  nand nand_207 (nand_207_out, Q66, CLK7);
  nand nand_208 (nand_208_out, not_56_out, CLK7);
  nand nand_209 (Q06, nand_193_out, Q7);
  nand nand_210 (Q7, Q06, nand_194_out);
  nand nand_211 (Q16, nand_195_out, Q15_2);
  nand nand_212 (Q15_2, Q16, nand_196_out);
  nand nand_213 (Q26_2, nand_197_out, Q23_2);
  nand nand_214 (Q23_2, Q26_2, nand_198_out);
  nand nand_215 (Q36, nand_199_out, Q31_2);
  nand nand_216 (Q31_2, Q36, nand_200_out);
  nand nand_217 (Q46_2, nand_201_out, Q39);
  nand nand_218 (Q39, Q46_2, nand_202_out);
  nand nand_219 (Q56, nand_203_out, Q47);
  nand nand_220 (Q47, Q56, nand_204_out);
  nand nand_221 (Q66, nand_205_out, Q55_2);
  nand nand_222 (Q55_2, Q66, nand_206_out);
  nand nand_223 (Q76, nand_207_out, Q63_2);
  nand nand_224 (Q63_2, Q76, nand_208_out);
  not not_57 (not_57_out, Data7);
  not not_58 (not_58_out, Q07);
  not not_59 (not_59_out, Q17_2);
  not not_60 (not_60_out, Q27_2);
  not not_61 (not_61_out, Q37);
  not not_62 (not_62_out, Q47_2);
  not not_63 (not_63_out, Q57_2);
  not not_64 (not_64_out, Q67);
  nand nand_225 (nand_225_out, Data7, CLK0);
  nand nand_226 (nand_226_out, not_57_out, CLK0);
  nand nand_227 (nand_227_out, Q07, CLK1);
  nand nand_228 (nand_228_out, not_58_out, CLK1);
  nand nand_229 (nand_229_out, Q17_2, CLK2);
  nand nand_230 (nand_230_out, not_59_out, CLK2);
  nand nand_231 (nand_231_out, Q27_2, CLK3);
  nand nand_232 (nand_232_out, not_60_out, CLK3);
  nand nand_233 (nand_233_out, Q37, CLK4);
  nand nand_234 (nand_234_out, not_61_out, CLK4);
  nand nand_235 (nand_235_out, Q47_2, CLK5);
  nand nand_236 (nand_236_out, not_62_out, CLK5);
  nand nand_237 (nand_237_out, Q57_2, CLK6);
  nand nand_238 (nand_238_out, not_63_out, CLK6);
  nand nand_239 (nand_239_out, Q67, CLK7);
  nand nand_240 (nand_240_out, not_64_out, CLK7);
  nand nand_241 (Q07, nand_225_out, Q8);
  nand nand_242 (Q8, Q07, nand_226_out);
  nand nand_243 (Q17_2, nand_227_out, Q16_2);
  nand nand_244 (Q16_2, Q17_2, nand_228_out);
  nand nand_245 (Q27_2, nand_229_out, Q24_2);
  nand nand_246 (Q24_2, Q27_2, nand_230_out);
  nand nand_247 (Q37, nand_231_out, Q32_2);
  nand nand_248 (Q32_2, Q37, nand_232_out);
  nand nand_249 (Q47_2, nand_233_out, Q40_2);
  nand nand_250 (Q40_2, Q47_2, nand_234_out);
  nand nand_251 (Q57_2, nand_235_out, Q48);
  nand nand_252 (Q48, Q57_2, nand_236_out);
  nand nand_253 (Q67, nand_237_out, Q56_2);
  nand nand_254 (Q56_2, Q67, nand_238_out);
  nand nand_255 (Q77, nand_239_out, Q64_2);
  nand nand_256 (Q64_2, Q77, nand_240_out);
endmodule
