// Digital circuit T-trigger.dig as structural Verilog
module T_trigger (
  input  in_3,
  input  in_4,
  output Q,
  output Q_2
);

  wire nand_1_out, nand_2_out;

  nand nand_1 (nand_1_out, Q_2, in_3, in_4);
  nand nand_2 (nand_2_out, in_4, in_3, Q);
  nand nand_3 (Q, nand_1_out, Q_2);
  nand nand_4 (Q_2, Q, nand_2_out);
endmodule
