// Digital circuit XOR.dig as structural Verilog
module XOR (
  input  in_1,
  input  in_2,
  output out_3
);

  wire nand_1_out, nand_2_out, nor_1_out, not_1_out, not_2_out, not_3_out, not_4_out;

  not not_1 (not_1_out, in_1);
  not not_2 (not_2_out, in_2);
  nand nand_1 (nand_1_out, in_1, not_2_out);
  nand nand_2 (nand_2_out, not_1_out, in_2);
  not not_3 (not_3_out, nand_1_out);
  not not_4 (not_4_out, nand_2_out);
  nor nor_1 (nor_1_out, not_3_out, not_4_out);
  not not_5 (out_3, nor_1_out);
endmodule
